// Logisim project MD-1_16b_CPU-Truth.circ as structural Verilog
module _74189_Ram (
  input  in_1,
  input  in_2,
  input  in_3,
  input  [3:0] in_4,
  input  [15:0] in_5,
  output [15:0] out_6
);

  wire not_1_out;
  wire [3:0] ram_1_data, ram_2_data, ram_3_data, ram_4_data;

  not not_1 (not_1_out, in_2);
  RAM #(.addrWidth(4), .dataWidth(4), .bus("separate")) ram_1 (
    .addr(in_4), .din(in_5[3:0]), .data(ram_1_data), .str(not_1_out), .sel(1'b1), .clk(not_1_out), .ld(in_3),
    .clr(in_1));
  RAM #(.addrWidth(4), .dataWidth(4), .bus("separate")) ram_2 (
    .addr(in_4), .din(in_5[7:4]), .data(ram_2_data), .str(not_1_out), .sel(1'b1), .clk(not_1_out), .ld(in_3),
    .clr(in_1));
  RAM #(.addrWidth(4), .dataWidth(4), .bus("separate")) ram_3 (
    .addr(in_4), .din(in_5[11:8]), .data(ram_3_data), .str(not_1_out), .sel(1'b1), .clk(not_1_out),
    .ld(in_3), .clr(in_1));
  RAM #(.addrWidth(4), .dataWidth(4), .bus("separate")) ram_4 (
    .addr(in_4), .din(in_5[15:12]), .data(ram_4_data), .str(not_1_out), .sel(1'b1), .clk(not_1_out),
    .ld(in_3), .clr(in_1));
  assign out_6 = in_3 ? {ram_4_data, ram_3_data, ram_2_data, ram_1_data} : 16'bz;  // Controlled_Buffer controlled_buffer_1

  // Notes on the sheet:
  //   Remember that in the 74189 it gives the complement
  //   I cannot make it give the complement in this simulation so in the real version i will need to invert
endmodule

module CPU (
  input  in_1,
  input  in_2,
  input  in_3,
  input  in_4,
  input  in_5,
  input  in_6,
  input  in_7,
  input  in_8,
  input  in_9,
  input  in_10,
  input  in_11,
  input  in_12,
  input  in_13,
  input  in_14,
  input  in_15,
  input  [3:0] in_16,
  input  [15:0] in_17,
  input  in_18,
  input  in_19,
  input  in_20,
  input  in_21
);

  wire CLKE, clock_1_out_6, dip_74157_1_p2, dip_74157_1_p3, dip_74157_1_p4, not_1_out;
  wire [3:0] a_register_1_out_5, mar_1_out_6, ram_io_mux_1_out_5;
  wire [15:0] ram_data_io_mux_1_out_5;
  wire [15:4] a_register_1_out_5_2;

  clock clock_1 (.Manual(in_3), .pulse(in_2), .Halt(in_5), .out_6(clock_1_out_6), .out_5(CLKE), .in_4(in_4));
  A_Register a_register_1 (
    .in_4({a_register_1_out_5_2, a_register_1_out_5}), .out_5({a_register_1_out_5_2, a_register_1_out_5}),
    .in_1(in_10), .in_2(clock_1_out_6), .in_3(in_9));  // open: out_6
  B_Register b_register_1 (
    .in_4({a_register_1_out_5_2, a_register_1_out_5}), .out_5({a_register_1_out_5_2, a_register_1_out_5}),
    .in_1(in_20), .in_2(clock_1_out_6), .in_3(in_21));  // open: out_6
  LED led_1 (.in(a_register_1_out_5_2[14]));
  LED led_2 (.in(a_register_1_out_5_2[15]));
  Pull_Resistor pull_resistor_1 (.node(a_register_1_out_5_2[15]));
  Pull_Resistor pull_resistor_2 (.node(a_register_1_out_5_2[14]));
  LED led_3 (.in(a_register_1_out_5_2[10]));
  LED led_4 (.in(a_register_1_out_5_2[11]));
  LED led_5 (.in(a_register_1_out_5_2[12]));
  LED led_6 (.in(a_register_1_out_5_2[13]));
  Pull_Resistor pull_resistor_3 (.node(a_register_1_out_5_2[11]));
  Pull_Resistor pull_resistor_4 (.node(a_register_1_out_5_2[13]));
  Pull_Resistor pull_resistor_5 (.node(a_register_1_out_5_2[12]));
  Pull_Resistor pull_resistor_6 (.node(a_register_1_out_5_2[10]));
  LED led_7 (.in(a_register_1_out_5_2[6]));
  LED led_8 (.in(a_register_1_out_5_2[7]));
  LED led_9 (.in(a_register_1_out_5_2[8]));
  LED led_10 (.in(a_register_1_out_5_2[9]));
  Pull_Resistor pull_resistor_7 (.node(a_register_1_out_5_2[7]));
  Pull_Resistor pull_resistor_8 (.node(a_register_1_out_5_2[9]));
  Pull_Resistor pull_resistor_9 (.node(a_register_1_out_5_2[8]));
  Pull_Resistor pull_resistor_10 (.node(a_register_1_out_5_2[6]));
  LED led_11 (.in(a_register_1_out_5_2[4]));
  LED led_12 (.in(a_register_1_out_5[2]));
  LED led_13 (.in(a_register_1_out_5[3]));
  LED led_14 (.in(a_register_1_out_5_2[5]));
  Pull_Resistor pull_resistor_11 (.node(a_register_1_out_5[3]));
  Pull_Resistor pull_resistor_12 (.node(a_register_1_out_5_2[4]));
  Pull_Resistor pull_resistor_13 (.node(a_register_1_out_5[2]));
  Pull_Resistor pull_resistor_14 (.node(a_register_1_out_5_2[5]));
  LED led_15 (.in(a_register_1_out_5[0]));
  LED led_16 (.in(a_register_1_out_5[1]));
  Pull_Resistor pull_resistor_15 (.node(a_register_1_out_5[1]));
  Pull_Resistor pull_resistor_16 (.node(a_register_1_out_5[0]));
  Program_Counter program_counter_1 (
    .in_4(a_register_1_out_5), .in_5(clock_1_out_6), .out_7(a_register_1_out_5), .in_3(in_1));  // open: in_1, in_6, in_2
  MAR mar_1 (
    .in_3(a_register_1_out_5), .in_4(clock_1_out_6), .in_5(in_6), .out_6(mar_1_out_6), .in_1(in_7),
    .in_2(in_8));
  Ram_DATA_IO_MUX ram_data_io_mux_1 (
    .in_3({a_register_1_out_5_2, a_register_1_out_5}), .in_4(in_17), .out_5(ram_data_io_mux_1_out_5),
    .in_1(not_1_out), .in_2(in_18));
  Ram_IO_MUX ram_io_mux_1 (
    .in_2(mar_1_out_6), .in_3(in_16), .out_5(ram_io_mux_1_out_5), .in_1(not_1_out), .in_4(in_11));
  _74189_Ram u_74189_ram_1 (
    .in_3(in_14), .in_2(dip_74157_1_p4), .in_4(ram_io_mux_1_out_5), .in_5(ram_data_io_mux_1_out_5),
    .out_6({a_register_1_out_5_2, a_register_1_out_5}), .in_1(in_13));
  not not_1 (not_1_out, in_12);
  // DIP_74157 dip_74157_1: pin names not known; wires that end beside it: in_12, dip_74157_1_p2, dip_74157_1_p3, dip_74157_1_p4, 1'b0
  // IC_7400 ic_7400_1: pin names not known; wires that end beside it: in_19, CLKE, dip_74157_1_p3, 1'b0
  not not_2 (dip_74157_1_p2, in_15);

  // Notes on the sheet:
  //   0 -> Program Mode , 1 Run Mode
  //   from the control logic
  //   Manual Write Enable
endmodule

module D_Flip_flop (
  input  in_1,
  input  in_2,
  input  data,
  output out_4
);

  wire and_1_out, and_2_out, nor_2_out, not_1_out;

  not not_1 (not_1_out, data);
  and and_1 (and_1_out, not_1_out, in_2);
  and and_2 (and_2_out, in_2, data);
  nor nor_1 (out_4, nor_2_out, in_1, and_1_out);
  nor nor_2 (nor_2_out, and_2_out, out_4);
endmodule

module _1_bit_Memory (
  input  in_1,
  input  in_2,
  input  in_3,
  input  in_4,
  output out_5
);

  wire and_1_out, and_2_out, not_1_out, or_1_out;

  not not_1 (not_1_out, in_3);
  and and_1 (and_1_out, not_1_out, out_5);
  or or_1 (or_1_out, and_1_out, and_2_out);
  and and_2 (and_2_out, in_3, in_4);
  D_Flip_flop d_flip_flop_1 (.out_4(out_5), .in_2(in_1), .data(or_1_out), .in_1(in_2));
endmodule

module _16_Bit_Reg (
  input  load,
  input  bus_en,
  input  clock,
  input  async,
  input  [15:0] in_5,
  output [15:0] out_6,
  output [15:0] out_7
);

  wire n1_bit_memory_1_out_5, n1_bit_memory_2_out_5, n1_bit_memory_3_out_5, n1_bit_memory_4_out_5,
       n1_bit_memory_5_out_5, n1_bit_memory_6_out_5, n1_bit_memory_7_out_5, n1_bit_memory_8_out_5,
       n1_bit_memory_9_out_5, n1_bit_memory_10_out_5, n1_bit_memory_11_out_5, n1_bit_memory_12_out_5,
       n1_bit_memory_13_out_5, n1_bit_memory_14_out_5, n1_bit_memory_15_out_5, n1_bit_memory_16_out_5,
       not_1_out, not_2_out;

  not not_1 (not_1_out, load);
  _1_bit_Memory u_1_bit_memory_1 (
    .in_3(not_1_out), .in_4(in_5[0]), .out_5(n1_bit_memory_1_out_5), .in_1(clock), .in_2(async));
  _1_bit_Memory u_1_bit_memory_2 (
    .in_3(not_1_out), .in_4(in_5[1]), .out_5(n1_bit_memory_2_out_5), .in_1(clock), .in_2(async));
  _1_bit_Memory u_1_bit_memory_3 (
    .in_3(not_1_out), .in_4(in_5[2]), .out_5(n1_bit_memory_3_out_5), .in_1(clock), .in_2(async));
  _1_bit_Memory u_1_bit_memory_4 (
    .in_3(not_1_out), .in_4(in_5[3]), .out_5(n1_bit_memory_4_out_5), .in_1(clock), .in_2(async));
  _1_bit_Memory u_1_bit_memory_5 (
    .in_3(not_1_out), .in_4(in_5[4]), .out_5(n1_bit_memory_5_out_5), .in_1(clock), .in_2(async));
  _1_bit_Memory u_1_bit_memory_6 (
    .in_3(not_1_out), .in_4(in_5[5]), .out_5(n1_bit_memory_6_out_5), .in_1(clock), .in_2(async));
  _1_bit_Memory u_1_bit_memory_7 (
    .in_3(not_1_out), .in_4(in_5[6]), .out_5(n1_bit_memory_7_out_5), .in_1(clock), .in_2(async));
  _1_bit_Memory u_1_bit_memory_8 (
    .in_3(not_1_out), .in_4(in_5[7]), .out_5(n1_bit_memory_8_out_5), .in_1(clock), .in_2(async));
  and and_1 (out_7[7], not_2_out, n1_bit_memory_8_out_5);
  and and_2 (out_7[0], not_2_out, n1_bit_memory_1_out_5);
  and and_3 (out_7[1], not_2_out, n1_bit_memory_2_out_5);
  and and_4 (out_7[2], not_2_out, n1_bit_memory_3_out_5);
  and and_5 (out_7[3], not_2_out, n1_bit_memory_4_out_5);
  and and_6 (out_7[4], not_2_out, n1_bit_memory_5_out_5);
  and and_7 (out_7[5], not_2_out, n1_bit_memory_6_out_5);
  and and_8 (out_7[6], not_2_out, n1_bit_memory_7_out_5);
  not not_2 (not_2_out, bus_en);
  and and_9 (out_7[8], not_2_out, n1_bit_memory_9_out_5);
  _1_bit_Memory u_1_bit_memory_9 (
    .in_3(not_1_out), .in_4(in_5[8]), .out_5(n1_bit_memory_9_out_5), .in_1(clock), .in_2(async));
  and and_10 (out_7[9], not_2_out, n1_bit_memory_10_out_5);
  _1_bit_Memory u_1_bit_memory_10 (
    .in_3(not_1_out), .in_4(in_5[9]), .out_5(n1_bit_memory_10_out_5), .in_1(clock), .in_2(async));
  and and_11 (out_7[10], not_2_out, n1_bit_memory_11_out_5);
  _1_bit_Memory u_1_bit_memory_11 (
    .in_3(not_1_out), .in_4(in_5[10]), .out_5(n1_bit_memory_11_out_5), .in_1(clock), .in_2(async));
  and and_12 (out_7[11], not_2_out, n1_bit_memory_12_out_5);
  _1_bit_Memory u_1_bit_memory_12 (
    .in_3(not_1_out), .in_4(in_5[11]), .out_5(n1_bit_memory_12_out_5), .in_1(clock), .in_2(async));
  and and_13 (out_7[12], not_2_out, n1_bit_memory_13_out_5);
  _1_bit_Memory u_1_bit_memory_13 (
    .in_3(not_1_out), .in_4(in_5[12]), .out_5(n1_bit_memory_13_out_5), .in_1(clock), .in_2(async));
  and and_14 (out_7[13], not_2_out, n1_bit_memory_14_out_5);
  _1_bit_Memory u_1_bit_memory_14 (
    .in_3(not_1_out), .in_4(in_5[13]), .out_5(n1_bit_memory_14_out_5), .in_1(clock), .in_2(async));
  and and_15 (out_7[14], not_2_out, n1_bit_memory_15_out_5);
  _1_bit_Memory u_1_bit_memory_15 (
    .in_3(not_1_out), .in_4(in_5[14]), .out_5(n1_bit_memory_15_out_5), .in_1(clock), .in_2(async));
  and and_16 (out_7[15], not_2_out, n1_bit_memory_16_out_5);
  _1_bit_Memory u_1_bit_memory_16 (
    .in_3(not_1_out), .in_4(in_5[15]), .out_5(n1_bit_memory_16_out_5), .in_1(clock), .in_2(async));
  assign out_6 = not_2_out ? out_7 : 16'bz;  // Controlled_Buffer controlled_buffer_1

  // Notes on the sheet:
  //   1-8
  //   9-16
endmodule

module clock (
  input  Manual,
  input  pulse,
  input  Halt,
  input  in_4,
  output out_5,
  output out_6
);

  wire and_1_out, and_2_out, and_3_out, and_4_out, clock_1_out, clock_2_out, not_1_out, not_2_out, not_3_out,
       or_1_out, or_2_out;

  Clock #(.highDuration(3), .lowDuration(5)) clock_1 (.out(clock_1_out));
  Clock #(.highDuration(4), .lowDuration(4)) clock_2 (.out(clock_2_out));
  not not_1 (not_1_out, clock_1_out);
  not not_2 (not_2_out, Manual);
  not not_3 (not_3_out, Halt);
  and and_1 (and_1_out, clock_2_out, not_2_out);
  and and_2 (and_2_out, Manual, pulse);
  and and_3 (and_3_out, Manual, in_4);
  and and_4 (and_4_out, not_1_out, and_1_out);
  or or_1 (or_1_out, and_4_out, and_3_out);
  or or_2 (or_2_out, and_1_out, and_2_out);
  and and_5 (out_5, or_1_out, not_3_out);
  and and_6 (out_6, or_2_out, not_3_out);

  // Notes on the sheet:
  //   Manual EN Pulse
endmodule

module Program_Counter (
  input  in_1,
  input  in_2,
  input  in_3,
  input  [3:0] in_4,
  input  in_5,
  input  in_6,
  output [3:0] out_7
);

  wire [3:0] ic_74161_1_p10;

  // IC_74161 ic_74161_1: pin names not known; wires that end beside it: in_4[0], in_4[1], in_4[2], in_4[3], in_5, in_1, in_2, in_6, in_2, ic_74161_1_p10[0], ic_74161_1_p10[1], ic_74161_1_p10[2], ic_74161_1_p10[3]
  assign out_7 = in_3 ? ic_74161_1_p10 : 4'bz;  // Controlled_Buffer controlled_buffer_1
endmodule

module Master_Slave_JK_Flip_Flop (
  input  in_1,
  input  in_2,
  input  in_3,
  input  in_4,
  output out_5,
  output out_6
);

  wire and_1_out, and_2_out, and_3_out, and_4_out, nor_1_out, nor_2_out, not_1_out;

  and and_1 (and_1_out, out_6, in_2, in_3);
  and and_2 (and_2_out, in_3, in_4, out_5);
  nor nor_1 (nor_1_out, and_1_out, in_1, nor_2_out);
  nor nor_2 (nor_2_out, nor_1_out, and_2_out);
  not not_1 (not_1_out, in_3);
  and and_3 (and_3_out, nor_1_out, not_1_out);
  and and_4 (and_4_out, not_1_out, nor_2_out);
  nor nor_3 (out_5, and_3_out, out_6);
  nor nor_4 (out_6, out_5, and_4_out);
endmodule

module A_Register (
  input  in_1,
  input  in_2,
  input  in_3,
  input  [15:0] in_4,
  output [15:0] out_5,
  output [15:0] out_6
);

  // IC_74173 ic_74173_1: pin names not known; wires that end beside it: in_4[0], in_4[1], in_4[2], in_4[3], in_2, in_1, out_6[0], out_6[1], out_6[2], out_6[3]
  // IC_74173 ic_74173_2: pin names not known; wires that end beside it: in_1, in_4[4], in_4[5], in_4[6], in_4[7], in_2, in_1, in_1, 1'b0, 1'b0, 1'b0, 1'b0, out_6[4], out_6[5], out_6[6], out_6[7]
  // IC_74173 ic_74173_3: pin names not known; wires that end beside it: in_4[8], in_4[9], in_4[10], in_4[11], in_2, in_1, out_6[8], out_6[9], out_6[10], out_6[11]
  // IC_74173 ic_74173_4: pin names not known; wires that end beside it: in_1, in_4[12], in_4[13], in_4[14], in_4[15], in_2, in_1, in_1, 1'b0, 1'b0, 1'b0, 1'b0, out_6[12], out_6[13], out_6[14], out_6[15]
  assign out_5 = in_3 ? out_6 : 16'bz;  // Controlled_Buffer controlled_buffer_1
endmodule

module B_Register (
  input  in_1,
  input  in_2,
  input  in_3,
  input  [15:0] in_4,
  output [15:0] out_5,
  output [15:0] out_6
);

  // IC_74173 ic_74173_1: pin names not known; wires that end beside it: in_4[0], in_4[1], in_4[2], in_4[3], in_2, in_1, out_6[0], out_6[1], out_6[2], out_6[3]
  // IC_74173 ic_74173_2: pin names not known; wires that end beside it: in_1, in_4[4], in_4[5], in_4[6], in_4[7], in_2, in_1, in_1, 1'b0, 1'b0, 1'b0, 1'b0, out_6[4], out_6[5], out_6[6], out_6[7]
  // IC_74173 ic_74173_3: pin names not known; wires that end beside it: in_4[8], in_4[9], in_4[10], in_4[11], in_2, in_1, out_6[8], out_6[9], out_6[10], out_6[11]
  // IC_74173 ic_74173_4: pin names not known; wires that end beside it: in_1, in_4[12], in_4[13], in_4[14], in_4[15], in_2, in_1, in_1, 1'b0, 1'b0, 1'b0, 1'b0, out_6[12], out_6[13], out_6[14], out_6[15]
  assign out_5 = in_3 ? out_6 : 16'bz;  // Controlled_Buffer controlled_buffer_1
endmodule

module _16_Bit_Adder (
  input  in_1,
  input  in_2,
  input  [15:0] in_3,
  input  [15:0] in_4,
  output [15:0] out_5
);

  wire ic_74283_2_p12, ic_74283_2_p18, ic_74283_4_p11, n4_bit_xor_1_out_6, n4_bit_xor_1_out_7,
       n4_bit_xor_1_out_8, n4_bit_xor_1_out_9, n4_bit_xor_2_out_6, n4_bit_xor_2_out_7, n4_bit_xor_2_out_8,
       n4_bit_xor_2_out_9, n4_bit_xor_3_out_6, n4_bit_xor_3_out_7, n4_bit_xor_3_out_8, n4_bit_xor_3_out_9,
       n4_bit_xor_4_out_6, n4_bit_xor_4_out_7, n4_bit_xor_4_out_8, n4_bit_xor_4_out_9;
  wire [15:0] ic_74283_1_p8;

  _4_Bit_Xor u_4_bit_xor_1 (
    .in_2(in_4[0]), .in_3(in_4[1]), .in_4(in_4[2]), .in_5(in_4[3]), .out_6(n4_bit_xor_1_out_6),
    .out_7(n4_bit_xor_1_out_7), .out_8(n4_bit_xor_1_out_8), .out_9(n4_bit_xor_1_out_9), .in_1(in_1));
  _4_Bit_Xor u_4_bit_xor_2 (
    .in_2(in_4[4]), .in_3(in_4[5]), .in_4(in_4[6]), .in_5(in_4[7]), .out_6(n4_bit_xor_2_out_6),
    .out_7(n4_bit_xor_2_out_7), .out_8(n4_bit_xor_2_out_8), .out_9(n4_bit_xor_2_out_9), .in_1(in_1));
  _4_Bit_Xor u_4_bit_xor_3 (
    .in_2(in_4[8]), .in_3(in_4[9]), .in_4(in_4[10]), .in_5(in_4[11]), .out_6(n4_bit_xor_3_out_6),
    .out_7(n4_bit_xor_3_out_7), .out_8(n4_bit_xor_3_out_8), .out_9(n4_bit_xor_3_out_9), .in_1(in_1));
  _4_Bit_Xor u_4_bit_xor_4 (
    .in_2(in_4[12]), .in_3(in_4[13]), .in_4(in_4[14]), .in_5(in_4[15]), .out_6(n4_bit_xor_4_out_6),
    .out_7(n4_bit_xor_4_out_7), .out_8(n4_bit_xor_4_out_8), .out_9(n4_bit_xor_4_out_9), .in_1(in_1));
  // IC_74283 ic_74283_1: pin names not known; wires that end beside it: in_3[0], in_3[1], in_3[2], in_3[3], n4_bit_xor_1_out_6, n4_bit_xor_1_out_7, n4_bit_xor_1_out_8, ic_74283_1_p8[0], ic_74283_1_p8[1], ic_74283_1_p8[2], ic_74283_1_p8[3]
  // IC_74283 ic_74283_2: pin names not known; wires that end beside it: in_4[3], n4_bit_xor_1_out_9, in_1, in_3[4], in_3[5], in_3[6], in_3[7], n4_bit_xor_2_out_6, n4_bit_xor_2_out_7, n4_bit_xor_2_out_8, n4_bit_xor_2_out_9, ic_74283_2_p12, ic_74283_2_p12, ic_74283_1_p8[4], ic_74283_1_p8[5], ic_74283_1_p8[6], ic_74283_1_p8[7], ic_74283_2_p18
  // IC_74283 ic_74283_3: pin names not known; wires that end beside it: in_3[8], in_3[9], in_3[10], in_3[11], n4_bit_xor_3_out_6, n4_bit_xor_3_out_7, n4_bit_xor_3_out_8, ic_74283_1_p8[8], ic_74283_1_p8[9], ic_74283_1_p8[10], ic_74283_1_p8[11]
  // IC_74283 ic_74283_4: pin names not known; wires that end beside it: n4_bit_xor_3_out_9, ic_74283_2_p18, in_3[12], in_3[13], in_3[14], in_3[15], n4_bit_xor_4_out_6, n4_bit_xor_4_out_7, n4_bit_xor_4_out_8, n4_bit_xor_4_out_9, ic_74283_4_p11, ic_74283_4_p11, ic_74283_1_p8[12], ic_74283_1_p8[13], ic_74283_1_p8[14], ic_74283_1_p8[15]
  assign out_5 = in_2 ? ic_74283_1_p8 : 16'bz;  // Controlled_Buffer controlled_buffer_1
endmodule

module _4_Bit_Xor (
  input  in_1,
  input  in_2,
  input  in_3,
  input  in_4,
  input  in_5,
  output out_6,
  output out_7,
  output out_8,
  output out_9
);

  xor xor_1 (out_6, in_2, in_1);
  xor xor_2 (out_7, in_3, in_1);
  xor xor_3 (out_8, in_4, in_1);
  xor xor_4 (out_9, in_5, in_1);
endmodule

module _16_Bit_Shifter_Right (
  input  in_1,
  input  [15:0] in_2,
  output [15:0] out_3
);

  wire [14:0] dip_74157_1_p4;

  // DIP_74157 dip_74157_1: pin names not known; wires that end beside it: 1'b1, in_2[0], in_2[1], dip_74157_1_p4[0], in_2[1], in_2[2], dip_74157_1_p4[1], 1'b0, in_2[3], in_2[4], dip_74157_1_p4[3], in_2[2], in_2[3], dip_74157_1_p4[2]
  // DIP_74157 dip_74157_2: pin names not known; wires that end beside it: 1'b1, in_2[4], in_2[5], dip_74157_1_p4[4], in_2[5], in_2[6], dip_74157_1_p4[5], 1'b0, in_2[7], in_2[8], dip_74157_1_p4[7], in_2[6], in_2[7], dip_74157_1_p4[6]
  // DIP_74157 dip_74157_3: pin names not known; wires that end beside it: 1'b1, in_2[8], in_2[9], dip_74157_1_p4[8], in_2[9], in_2[10], dip_74157_1_p4[9], 1'b0, in_2[11], in_2[12], dip_74157_1_p4[11], in_2[10], in_2[11], dip_74157_1_p4[10]
  // DIP_74157 dip_74157_4: pin names not known; wires that end beside it: 1'b1, in_2[12], in_2[13], dip_74157_1_p4[12], in_2[13], in_2[14], dip_74157_1_p4[13], 1'b0, 1'b0, 1'b0, in_2[14], 1'b0, dip_74157_1_p4[14]
  assign out_3 = in_1 ? {in_2[15], dip_74157_1_p4} : 16'bz;  // Controlled_Buffer controlled_buffer_1
endmodule

module ALU (
  input  [2:0] in_1
);

  wire dip_74138_1_p7, dip_74138_1_p8, dip_74138_1_p9, dip_74138_1_p10, dip_74138_1_p11, dip_74138_1_p12,
       dip_74138_1_p13, dip_74138_1_p14, ic_7404_1_p5, ic_7404_1_p6, ic_7404_1_p7, ic_7404_1_p8,
       ic_7404_2_p5, ic_7404_2_p6;

  // DIP_74138 dip_74138_1: pin names not known; wires that end beside it: in_1[0], in_1[1], in_1[2], 1'b0, 1'b0, 1'b1, dip_74138_1_p7, dip_74138_1_p8, dip_74138_1_p9, dip_74138_1_p10, dip_74138_1_p11, dip_74138_1_p12, dip_74138_1_p13, dip_74138_1_p14
  // IC_7404 ic_7404_1: pin names not known; wires that end beside it: dip_74138_1_p8, dip_74138_1_p9, dip_74138_1_p10, dip_74138_1_p11, ic_7404_1_p5, ic_7404_1_p6, ic_7404_1_p7, ic_7404_1_p8, ic_7404_1_p8, ic_7404_1_p7, ic_7404_1_p6, ic_7404_1_p5
  // IC_7404 ic_7404_2: pin names not known; wires that end beside it: dip_74138_1_p12, dip_74138_1_p13, dip_74138_1_p14, dip_74138_1_p7, ic_7404_2_p5, ic_7404_2_p6, ic_7404_2_p6, ic_7404_2_p5

  // Notes on the sheet:
  //   0000 ADD
  //   0001 SUB
  //   0010 MUL
  //   0011 DIV
  //   OP SRC DES IMM
  //   0100 SHR
  //   0101 SHL
  //   0110 IMM
  //   0111 JUMP
  //   1000 LDA
  //   1001 LDB
  //   1010LDC
  //   1011LDD
endmodule

module Ram_IO_MUX (
  input  in_1,
  input  [3:0] in_2,
  input  [3:0] in_3,
  input  in_4,
  output [3:0] out_5
);

  // IC_74157 ic_74157_1: pin names not known; wires that end beside it: in_2[0], in_3[0], in_2[1], in_3[1], in_2[2], in_3[2], in_2[3], in_3[3], in_1, in_4, out_5[0], out_5[1], out_5[2], out_5[3]
endmodule

module MAR (
  input  in_1,
  input  in_2,
  input  [3:0] in_3,
  input  in_4,
  input  in_5,
  output [3:0] out_6
);

  // IC_74173 ic_74173_1: pin names not known; wires that end beside it: in_3[0], in_3[1], in_3[2], in_3[3], in_4, in_1, in_1, in_5, in_2, in_2, out_6[0], out_6[1], out_6[2], out_6[3]
endmodule

module Ram_DATA_IO_MUX (
  input  in_1,
  input  in_2,
  input  [15:0] in_3,
  input  [15:0] in_4,
  output [15:0] out_5
);

  // IC_74157 ic_74157_1: pin names not known; wires that end beside it: in_3[0], in_4[0], in_3[1], in_4[1], in_3[2], in_4[2], in_1, out_5[0], out_5[1], out_5[2]
  // IC_74157 ic_74157_2: pin names not known; wires that end beside it: in_3[3], in_4[3], in_3[4], in_4[4], in_3[5], in_4[5], in_3[6], in_4[6], in_2, in_1, out_5[3], out_5[4], out_5[5], out_5[6]
  // IC_74157 ic_74157_3: pin names not known; wires that end beside it: in_3[7], in_4[7], in_3[8], in_4[8], in_3[9], in_4[9], in_3[10], in_4[10], in_2, in_1, out_5[7], out_5[8], out_5[9], out_5[10]
  // IC_74157 ic_74157_4: pin names not known; wires that end beside it: in_3[11], in_4[11], in_3[12], in_4[12], in_3[13], in_4[13], in_3[14], in_4[14], in_3[15], in_4[15], in_2, in_1, in_2, out_5[11], out_5[12], out_5[13], out_5[14], out_5[15]
endmodule

module testing (
  input  in_1,
  input  in_2,
  input  in_3,
  input  [10:0] in_4,
  input  [15:0] in_5,
  output [15:0] out_6
);

  EEPROM eeprom_1 (.in_4(in_4), .in_5(in_5), .out_6(out_6), .in_2(in_1), .in_3(in_2), .in_1(in_3));
endmodule

module EEPROM (
  input  in_1,
  input  in_2,
  input  in_3,
  input  [10:0] in_4,
  input  [15:0] in_5,
  output [15:0] out_6
);

  wire not_1_out, not_2_out;
  wire [7:0] ram_1_data, ram_2_data;

  not not_1 (not_1_out, in_3);
  RAM #(.addrWidth(11), .bus("separate")) ram_1 (
    .addr(in_4), .din(in_5[7:0]), .data(ram_1_data), .str(not_1_out), .sel(1'b1), .clk(not_1_out),
    .ld(not_2_out), .clr(in_2));
  RAM #(.addrWidth(11), .bus("separate")) ram_2 (
    .addr(in_4), .din(in_5[15:8]), .data(ram_2_data), .str(not_1_out), .sel(1'b1), .clk(not_1_out),
    .ld(not_2_out), .clr(in_2));
  not not_2 (not_2_out, in_1);
  assign out_6 = not_2_out ? {ram_2_data, ram_1_data} : 16'bz;  // Controlled_Buffer controlled_buffer_1
endmodule

module Arithmetic_Unit (
  input  [15:0] in_1,
  input  [15:0] in_2,
  input  in_3,
  input  in_4,
  input  in_5
);

  wire [15:0] controlled_buffer_1_out, controlled_buffer_2_out, controlled_buffer_3_out;

  assign controlled_buffer_1_out = in_4 ? in_1 : 16'bz;  // Controlled_Buffer controlled_buffer_1
  assign controlled_buffer_2_out = in_4 ? in_2 : 16'bz;  // Controlled_Buffer controlled_buffer_2
  assign controlled_buffer_3_out = in_5 ? in_2 : 16'bz;  // Controlled_Buffer controlled_buffer_3
  _16_Bit_Shifter_Right u_16_bit_shifter_right_1 (.in_2(controlled_buffer_3_out), .in_1(in_5));  // open: out_3
  _16_Bit_Adder u_16_bit_adder_1 (
    .in_3(controlled_buffer_1_out), .in_4(controlled_buffer_2_out), .in_1(in_3), .in_2(1'b0));  // open: out_5
endmodule

module _16_Bit_Shifter_Left (
  input  [15:0] in_1,
  output [15:0] out_2
);

  _16_Bit_Adder u_16_bit_adder_1 (.out_5(out_2), .in_2(1'b0));  // open: in_3, in_4, in_1
endmodule
