// Logisim project MD-1_16b_CPU.circ as structural Verilog: 29 circuits, main circuit L_74189_Ram
module L_74189_Ram (
  input  in_1,
  input  in_2,
  input  [15:0] in_3,
  input  [15:0] in_4,
  output [15:0] out_5,
  output [15:0] out_6
);

  wire not_1_out;

  not not_1 (not_1_out, in_2);
  RAM #(.addrWidth(16), .dataWidth(16), .enables("line")) ram_1 (
    .addr(in_3), .we(not_1_out), .clk(not_1_out), .din(in_4), .dout(out_6));
  assign out_5 = in_1 ? out_6 : 16'bz;  // Controlled_Buffer controlled_buffer_1
endmodule

module CPU (
  input  in_1,
  input  in_2,
  input  in_3,
  input  [15:0] in_4,
  input  [15:0] in_5,
  input  in_6,
  input  in_7,
  input  in_8,
  input  in_9,
  input  in_10,
  input  in_11
);

  wire A_I, A_O, ALU_O, B_I, B_O, CLK, CLKE, CNT_E, CNT_O, control_unit_1_a_i, control_unit_1_b_i,
       control_unit_1_ir_i, control_unit_1_jump, control_unit_1_mar_i, control_unit_1_o_i, HLT, IR_I, IR_O,
       JMP, MAR_I, not_1_out, not_2_out, not_3_out, not_4_out, not_5_out, not_6_out, OUT_I, RAM_I, RAM_O,
       SIGN, SUB;
  wire [3:0] HUNS, INSTRUCTION, ONES, TENS, THOU, TTHOU;
  wire [7:0] IR, Stepper;
  wire [15:0] A_REG, ADR, alu_1_out_6, B_REG, BUS, DATA, mar_1_out_5, OUT_O, PC, RAM, undriven, undriven_2;

  LED led_1 (.in(A_REG[15]));
  LED led_2 (.in(A_REG[14]));
  LED led_3 (.in(A_REG[13]));
  LED led_4 (.in(B_REG[15]));
  LED led_5 (.in(B_REG[14]));
  LED led_6 (.in(B_REG[13]));
  LED led_7 (.in(undriven[15]));
  LED led_8 (.in(undriven[14]));
  LED led_9 (.in(undriven[13]));
  LED led_10 (.in(DATA[15]));
  LED led_11 (.in(DATA[14]));
  LED led_12 (.in(DATA[13]));
  LED led_13 (.in(BUS[15]));
  LED led_14 (.in(BUS[14]));
  LED led_15 (.in(BUS[13]));
  LED led_16 (.in(OUT_O[15]));
  LED led_17 (.in(OUT_O[14]));
  LED led_18 (.in(OUT_O[13]));
  LED led_19 (.in(PC[15]));
  LED led_20 (.in(PC[14]));
  LED led_21 (.in(PC[13]));
  LED led_22 (.in(A_REG[11]));
  LED led_23 (.in(A_REG[10]));
  LED led_24 (.in(A_REG[9]));
  LED led_25 (.in(A_REG[12]));
  LED led_26 (.in(B_REG[11]));
  LED led_27 (.in(B_REG[10]));
  LED led_28 (.in(B_REG[9]));
  LED led_29 (.in(B_REG[12]));
  LED led_30 (.in(undriven[11]));
  LED led_31 (.in(undriven[10]));
  LED led_32 (.in(undriven[9]));
  LED led_33 (.in(undriven[12]));
  LED led_34 (.in(DATA[11]));
  LED led_35 (.in(DATA[10]));
  LED led_36 (.in(DATA[9]));
  LED led_37 (.in(DATA[12]));
  LED led_38 (.in(BUS[11]));
  LED led_39 (.in(BUS[10]));
  LED led_40 (.in(BUS[9]));
  LED led_41 (.in(BUS[12]));
  LED led_42 (.in(OUT_O[11]));
  LED led_43 (.in(OUT_O[10]));
  LED led_44 (.in(OUT_O[9]));
  LED led_45 (.in(OUT_O[12]));
  LED led_46 (.in(PC[11]));
  LED led_47 (.in(PC[10]));
  LED led_48 (.in(PC[9]));
  LED led_49 (.in(PC[12]));
  clock clock_1 (.Manual(in_8), .pulse(in_7), .Halt(HLT), .in_4(in_9), .out_6(CLK), .out_5(CLKE));
  LED led_50 (.in(A_REG[8]));
  LED led_51 (.in(A_REG[7]));
  LED led_52 (.in(A_REG[6]));
  LED led_53 (.in(A_REG[5]));
  LED led_54 (.in(B_REG[8]));
  LED led_55 (.in(B_REG[7]));
  LED led_56 (.in(B_REG[6]));
  LED led_57 (.in(B_REG[5]));
  LED led_58 (.in(undriven[8]));
  LED led_59 (.in(undriven[7]));
  LED led_60 (.in(undriven[6]));
  LED led_61 (.in(undriven[5]));
  LED led_62 (.in(DATA[8]));
  LED led_63 (.in(DATA[7]));
  LED led_64 (.in(DATA[6]));
  LED led_65 (.in(DATA[5]));
  LED led_66 (.in(BUS[8]));
  LED led_67 (.in(BUS[7]));
  LED led_68 (.in(BUS[6]));
  LED led_69 (.in(BUS[5]));
  LED led_70 (.in(OUT_O[8]));
  LED led_71 (.in(OUT_O[7]));
  LED led_72 (.in(OUT_O[6]));
  LED led_73 (.in(OUT_O[5]));
  LED led_74 (.in(PC[8]));
  LED led_75 (.in(PC[7]));
  LED led_76 (.in(PC[6]));
  LED led_77 (.in(PC[5]));
  LED led_78 (.in(A_REG[4]));
  LED led_79 (.in(A_REG[3]));
  LED led_80 (.in(A_REG[2]));
  LED led_81 (.in(A_REG[1]));
  LED led_82 (.in(B_REG[4]));
  LED led_83 (.in(B_REG[3]));
  LED led_84 (.in(B_REG[2]));
  LED led_85 (.in(B_REG[1]));
  LED led_86 (.in(undriven[4]));
  LED led_87 (.in(undriven[3]));
  LED led_88 (.in(undriven[2]));
  LED led_89 (.in(undriven[1]));
  LED led_90 (.in(DATA[4]));
  LED led_91 (.in(DATA[3]));
  LED led_92 (.in(DATA[2]));
  LED led_93 (.in(DATA[1]));
  LED led_94 (.in(BUS[4]));
  LED led_95 (.in(BUS[3]));
  LED led_96 (.in(BUS[2]));
  LED led_97 (.in(BUS[1]));
  LED led_98 (.in(OUT_O[4]));
  LED led_99 (.in(OUT_O[3]));
  LED led_100 (.in(OUT_O[2]));
  LED led_101 (.in(OUT_O[1]));
  LED led_102 (.in(PC[4]));
  LED led_103 (.in(PC[3]));
  LED led_104 (.in(PC[2]));
  LED led_105 (.in(PC[1]));
  LED led_106 (.in(A_REG[0]));
  LED led_107 (.in(B_REG[0]));
  LED led_108 (.in(IR[7]));
  LED led_109 (.in(IR[6]));
  LED led_110 (.in(undriven[0]));
  LED led_111 (.in(RAM[15]));
  LED led_112 (.in(RAM[14]));
  LED led_113 (.in(RAM[13]));
  LED led_114 (.in(DATA[0]));
  LED led_115 (.in(ADR[15]));
  LED led_116 (.in(ADR[14]));
  LED led_117 (.in(ADR[13]));
  LED led_118 (.in(BUS[0]));
  LED led_119 (.in(undriven_2[15]));
  LED led_120 (.in(undriven_2[14]));
  LED led_121 (.in(OUT_O[0]));
  LED led_122 (.in(PC[0]));
  LED led_123 (.in(IR[5]));
  LED led_124 (.in(IR[4]));
  LED led_125 (.in(IR[3]));
  LED led_126 (.in(IR[2]));
  LED led_127 (.in(RAM[12]));
  LED led_128 (.in(RAM[11]));
  LED led_129 (.in(RAM[10]));
  LED led_130 (.in(RAM[9]));
  LED led_131 (.in(ADR[12]));
  LED led_132 (.in(ADR[11]));
  LED led_133 (.in(ADR[10]));
  LED led_134 (.in(ADR[9]));
  LED led_135 (.in(undriven_2[13]));
  LED led_136 (.in(undriven_2[12]));
  LED led_137 (.in(undriven_2[11]));
  LED led_138 (.in(undriven_2[10]));
  LED led_139 (.in(IR[1]));
  LED led_140 (.in(IR[0]));
  LED led_141 (.in(RAM[8]));
  LED led_142 (.in(RAM[7]));
  LED led_143 (.in(RAM[6]));
  LED led_144 (.in(RAM[5]));
  LED led_145 (.in(ADR[8]));
  LED led_146 (.in(ADR[7]));
  LED led_147 (.in(ADR[6]));
  LED led_148 (.in(ADR[5]));
  LED led_149 (.in(undriven_2[9]));
  LED led_150 (.in(undriven_2[8]));
  LED led_151 (.in(undriven_2[7]));
  LED led_152 (.in(undriven_2[6]));
  A_Register a_register_1 (.in_4(BUS), .in_1(A_I), .in_2(CLKE), .BUS_EN(A_O), .out_5(BUS), .out_6(A_REG));
  ALU alu_1 (.in_3(A_REG), .in_4(B_REG), .in_1(SUB), .in_2(ALU_O), .out_6(alu_1_out_6), .out_5(BUS));
  B_Register b_register_1 (.in_4(BUS), .in_1(B_I), .in_2(CLKE), .in_3(B_O), .out_5(BUS), .out_6(B_REG));
  LED led_153 (.in(RAM[4]));
  LED led_154 (.in(RAM[3]));
  LED led_155 (.in(RAM[2]));
  LED led_156 (.in(RAM[1]));
  LED led_157 (.in(ADR[4]));
  LED led_158 (.in(ADR[3]));
  LED led_159 (.in(ADR[2]));
  LED led_160 (.in(ADR[1]));
  LED led_161 (.in(undriven_2[5]));
  LED led_162 (.in(undriven_2[4]));
  LED led_163 (.in(undriven_2[3]));
  LED led_164 (.in(undriven_2[2]));
  LED led_165 (.in(Stepper[0]));
  LED led_166 (.in(Stepper[1]));
  LED led_167 (.in(RAM[0]));
  LED led_168 (.in(ADR[0]));
  Pull_Resistor pull_resistor_1 (.node(BUS[15]));
  Pull_Resistor pull_resistor_2 (.node(BUS[14]));
  LED led_169 (.in(undriven_2[1]));
  LED led_170 (.in(undriven_2[0]));
  LED led_171 (.in(Stepper[2]));
  LED led_172 (.in(Stepper[3]));
  LED led_173 (.in(Stepper[4]));
  LED led_174 (.in(Stepper[5]));
  Pull_Resistor pull_resistor_3 (.node(BUS[13]));
  Pull_Resistor pull_resistor_4 (.node(BUS[12]));
  Pull_Resistor pull_resistor_5 (.node(BUS[11]));
  Pull_Resistor pull_resistor_6 (.node(BUS[10]));
  LED led_175 (.in(Stepper[6]));
  LED led_176 (.in(Stepper[7]));
  Pull_Resistor pull_resistor_7 (.node(BUS[9]));
  Pull_Resistor pull_resistor_8 (.node(BUS[8]));
  Pull_Resistor pull_resistor_9 (.node(BUS[7]));
  Pull_Resistor pull_resistor_10 (.node(BUS[6]));
  LED led_177 (.in(HLT));
  _7_Segment_Display u_7_segment_display_1 (.g(SIGN));  // open: f, a, b, e, d, c, dp
  Hex_Digit_Display hex_digit_display_1 (.value(TTHOU));  // open: dp
  Pull_Resistor pull_resistor_11 (.node(BUS[5]));
  Pull_Resistor pull_resistor_12 (.node(BUS[4]));
  Pull_Resistor pull_resistor_13 (.node(BUS[3]));
  Pull_Resistor pull_resistor_14 (.node(BUS[2]));
  LED led_178 (.in(not_1_out));
  LED led_179 (.in(RAM_I));
  not not_1 (not_1_out, MAR_I);
  Hex_Digit_Display hex_digit_display_2 (.value(THOU));  // open: dp
  Hex_Digit_Display hex_digit_display_3 (.value(HUNS));  // open: dp
  Pull_Resistor pull_resistor_15 (.node(BUS[1]));
  Pull_Resistor pull_resistor_16 (.node(BUS[0]));
  LED led_180 (.in(not_2_out));
  LED led_181 (.in(RAM_O));
  not not_2 (not_2_out, A_I);
  Hex_Digit_Display hex_digit_display_4 (.value(ONES));  // open: dp
  Hex_Digit_Display hex_digit_display_5 (.value(TENS));  // open: dp
  LED led_182 (.in(A_O));
  LED led_183 (.in(not_3_out));
  not not_3 (not_3_out, B_I);
  LED led_184 (.in(B_O));
  LED led_185 (.in(ALU_O));
  Program_Counter program_counter_1 (
    .in_5(CNT_O), .I(BUS), .CLK(CLKE), .CLR(not_6_out), .LE(JMP), .COUNT_EN(CNT_E), .O(BUS), .ALO(PC));
  MEM_UNIT mem_unit_1 (
    .DATA_OE_LOW(1'b0), .ADR_OE_LOW(1'b0), .RAM_O(RAM_O), .PRG_RUN(in_6), .MANUAL_W(in_3), .RAM_I(RAM_I),
    .CLKE(CLKE), .DATA_A(BUS), .DATA_B(in_5), .ADR_A(mar_1_out_5), .ADR_B(in_4), .O(BUS), .ALO(RAM),
    .ADR(ADR), .out_13(DATA));
  LED led_186 (.in(SUB));
  LED led_187 (.in(IR_O));
  LED led_188 (.in(not_4_out));
  not not_4 (not_4_out, IR_I);
  MAR mar_1 (.in_1(MAR_I), .in_4(in_1), .in_3(CLK), .out_5(mar_1_out_5));  // open: in_2
  Instruction_Register instruction_register_1 (
    .in_5(BUS[7:0]), .in_1(in_10), .in_2(IR_I), .in_3(CLKE), .in_4(IR_O), .out_7(IR), .out_6(BUS[3:0]),
    .out_8(INSTRUCTION));
  OUT_REG out_reg_1 (.in_3(BUS), .in_1(OUT_I), .in_2(CLK), .out_4(OUT_O));
  LED led_189 (.in(CNT_E));
  Flags_Register flags_register_1 (.in_3(BUS[3:0]));  // open: in_1, in_2, in_4, out_5
  LED led_190 (.in(CNT_O));
  LED led_191 (.in(not_5_out));
  not not_5 (not_5_out, JMP);
  not not_6 (not_6_out, in_2);
  ROM_DIS rom_dis_1 (
    .in_1(in_11), .in_2(OUT_O), .out_3(SIGN), .out_4(TTHOU), .out_5(THOU), .out_6(HUNS), .out_7(TENS),
    .out_8(ONES));
  Control_unit control_unit_1 (
    .INSTRUCTION(INSTRUCTION), .CLK(CLK), .HLT(HLT), .MAR_I(control_unit_1_mar_i), .RAM_I(RAM_I),
    .RAM_O(RAM_O), .IR_0(IR_O), .IR_I(control_unit_1_ir_i), .A_I(control_unit_1_a_i), .A_O(A_O),
    .ALU_O(ALU_O), .SUB(SUB), .B_I(control_unit_1_b_i), .O_I(control_unit_1_o_i), .CE(CNT_E), .C0(CNT_O),
    .JUMP(control_unit_1_jump), .B_O(B_O), .STEP(Stepper));
  not not_7 (MAR_I, control_unit_1_mar_i);
  not not_8 (IR_I, control_unit_1_ir_i);
  not not_9 (A_I, control_unit_1_a_i);
  not not_10 (B_I, control_unit_1_b_i);
  not not_11 (OUT_I, control_unit_1_o_i);
  not not_12 (JMP, control_unit_1_jump);

  // Other names for the same wires on the sheet: Manual_ADR[15:0] = in_4; Manual_DATA[15:0] = in_5; Manual_W = in_3;
  //   PRG_RUN = in_6; TWO_CMP = in_11

  // Notes on the sheet:
  //   To Controller
  //   Manual Write Enable
  //   0 -> Program Mode , 1 Run Mode
endmodule

module clock (
  input  Manual,
  input  pulse,
  input  Halt,
  input  in_4,
  output out_5,
  output out_6
);

  wire and_1_out, and_2_out, and_3_out, and_4_out, clock_1_out, clock_2_out, not_1_out, not_2_out, not_3_out,
       or_1_out, or_2_out;

  Clock #(.lowDuration(3)) clock_1 (.out(clock_1_out));
  Clock #(.highDuration(2), .lowDuration(2)) clock_2 (.out(clock_2_out));
  not not_1 (not_1_out, clock_1_out);
  not not_2 (not_2_out, Manual);
  not not_3 (not_3_out, Halt);
  and and_1 (and_1_out, clock_2_out, not_2_out);
  and and_2 (and_2_out, Manual, pulse);
  and and_3 (and_3_out, Manual, in_4);
  and and_4 (and_4_out, not_1_out, and_1_out);
  or or_1 (or_1_out, and_4_out, and_3_out);
  or or_2 (or_2_out, and_1_out, and_2_out);
  and and_5 (out_5, or_1_out, not_3_out);
  and and_6 (out_6, or_2_out, not_3_out);

  // Notes on the sheet:
  //   Manual EN Pulse
endmodule

module Program_Counter (
  input  CLK,
  input  CLR,
  input  LE,
  input  COUNT_EN,
  input  in_5,
  input  [15:0] I,
  output [15:0] O,
  output [15:0] ALO
);

  wire c_74161_1_tc, c_74161_2_tc, c_74161_3_tc;

  C_74161 c_74161_1 (
    .CLK(CLK), .CLR(CLR), .LE(LE), .CEP(COUNT_EN), .CET(COUNT_EN), .D1(I[0]), .D2(I[1]), .D3(I[2]),
    .D4(I[3]), .Q1(ALO[0]), .Q2(ALO[1]), .Q3(ALO[2]), .Q4(ALO[3]), .TC(c_74161_1_tc));
  C_74161 c_74161_2 (
    .CLK(c_74161_1_tc), .CLR(CLR), .LE(LE), .CEP(COUNT_EN), .CET(COUNT_EN), .D1(I[4]), .D2(I[5]), .D3(I[6]),
    .D4(I[7]), .Q1(ALO[4]), .Q2(ALO[5]), .Q3(ALO[6]), .Q4(ALO[7]), .TC(c_74161_2_tc));
  C_74161 c_74161_3 (
    .CLK(c_74161_2_tc), .CLR(CLR), .LE(LE), .CEP(COUNT_EN), .CET(COUNT_EN), .D1(I[8]), .D2(I[9]), .D3(I[10]),
    .D4(I[11]), .Q1(ALO[8]), .Q2(ALO[9]), .Q3(ALO[10]), .Q4(ALO[11]), .TC(c_74161_3_tc));
  C_74161 c_74161_4 (
    .CLK(c_74161_3_tc), .CLR(CLR), .LE(LE), .CEP(COUNT_EN), .CET(COUNT_EN), .D1(I[12]), .D2(I[13]),
    .D3(I[14]), .D4(I[15]), .Q1(ALO[12]), .Q2(ALO[13]), .Q3(ALO[14]), .Q4(ALO[15]));  // open: TC
  assign O = in_5 ? ALO : 16'bz;  // Controlled_Buffer controlled_buffer_1
endmodule

module A_Register (
  input  in_1,
  input  in_2,
  input  BUS_EN,
  input  [15:0] in_4,
  output [15:0] out_5,
  output [15:0] out_6
);

  C_74173 c_74173_1 (
    .D2(in_4[1]), .D3(in_4[2]), .D1(in_4[0]), .D4(in_4[3]), .CLK(in_2), .CE1(in_1), .CE2(in_1), .OE1(1'b0),
    .OE2(1'b0), .Q2(out_6[1]), .Q3(out_6[2]), .Q1(out_6[0]), .Q4(out_6[3]));  // open: CLR
  C_74173 c_74173_2 (
    .D2(in_4[5]), .D3(in_4[6]), .D1(in_4[4]), .D4(in_4[7]), .CLK(in_2), .CE1(in_1), .CE2(in_1), .OE1(1'b0),
    .OE2(1'b0), .Q2(out_6[5]), .Q3(out_6[6]), .Q1(out_6[4]), .Q4(out_6[7]));  // open: CLR
  C_74173 c_74173_3 (
    .D2(in_4[9]), .D3(in_4[10]), .D1(in_4[8]), .D4(in_4[11]), .CLK(in_2), .CE1(in_1), .CE2(in_1), .OE1(1'b0),
    .OE2(1'b0), .Q2(out_6[9]), .Q3(out_6[10]), .Q1(out_6[8]), .Q4(out_6[11]));  // open: CLR
  C_74173 c_74173_4 (
    .D2(in_4[13]), .D3(in_4[14]), .D1(in_4[12]), .D4(in_4[15]), .CLK(in_2), .CE1(in_1), .CE2(in_1),
    .OE1(1'b0), .OE2(1'b0), .Q2(out_6[13]), .Q3(out_6[14]), .Q1(out_6[12]), .Q4(out_6[15]));  // open: CLR
  assign out_5 = BUS_EN ? out_6 : 16'bz;  // Controlled_Buffer controlled_buffer_1
endmodule

module B_Register (
  input  in_1,
  input  in_2,
  input  in_3,
  input  [15:0] in_4,
  output [15:0] out_5,
  output [15:0] out_6
);

  C_74173 c_74173_1 (
    .D2(in_4[1]), .D3(in_4[2]), .D1(in_4[0]), .D4(in_4[3]), .CLK(in_2), .CE1(in_1), .CE2(in_1), .OE1(1'b0),
    .OE2(1'b0), .Q2(out_6[1]), .Q3(out_6[2]), .Q1(out_6[0]), .Q4(out_6[3]));  // open: CLR
  C_74173 c_74173_2 (
    .D2(in_4[5]), .D3(in_4[6]), .D1(in_4[4]), .D4(in_4[7]), .CLK(in_2), .CE1(in_1), .CE2(in_1), .OE1(1'b0),
    .OE2(1'b0), .Q2(out_6[5]), .Q3(out_6[6]), .Q1(out_6[4]), .Q4(out_6[7]));  // open: CLR
  C_74173 c_74173_3 (
    .D2(in_4[9]), .D3(in_4[10]), .D1(in_4[8]), .D4(in_4[11]), .CLK(in_2), .CE1(in_1), .CE2(in_1), .OE1(1'b0),
    .OE2(1'b0), .Q2(out_6[9]), .Q3(out_6[10]), .Q1(out_6[8]), .Q4(out_6[11]));  // open: CLR
  C_74173 c_74173_4 (
    .D2(in_4[13]), .D3(in_4[14]), .D1(in_4[12]), .D4(in_4[15]), .CLK(in_2), .CE1(in_1), .CE2(in_1),
    .OE1(1'b0), .OE2(1'b0), .Q2(out_6[13]), .Q3(out_6[14]), .Q1(out_6[12]), .Q4(out_6[15]));  // open: CLR
  assign out_5 = in_3 ? out_6 : 16'bz;  // Controlled_Buffer controlled_buffer_1
endmodule

module L_16_Bit_Adder (
  input  in_1,
  input  [15:0] in_2,
  input  [15:0] in_3,
  output [15:0] out_4
);

  wire _7486_XOR_out_6, _7486_XOR_out_7, _7486_XOR_out_8, _7486_XOR_out_9, l_4_bit_xor_1_out_6,
       l_4_bit_xor_1_out_7, l_4_bit_xor_1_out_8, l_4_bit_xor_1_out_9, l_4_bit_xor_2_out_6,
       l_4_bit_xor_2_out_7, l_4_bit_xor_2_out_8, l_4_bit_xor_2_out_9, l_4_bit_xor_3_out_6,
       l_4_bit_xor_3_out_7, l_4_bit_xor_3_out_8, l_4_bit_xor_3_out_9, l_4b_add_1_cout, l_4b_add_2_cout,
       l_4b_add_3_cout;

  L_4_Bit_Xor _7486_XOR (
    .in_2(in_3[0]), .in_3(in_3[1]), .in_4(in_3[2]), .in_5(in_3[3]), .in_1(in_1), .out_6(_7486_XOR_out_6),
    .out_7(_7486_XOR_out_7), .out_8(_7486_XOR_out_8), .out_9(_7486_XOR_out_9));
  L_4_Bit_Xor l_4_bit_xor_1 (
    .in_2(in_3[4]), .in_3(in_3[5]), .in_4(in_3[6]), .in_5(in_3[7]), .in_1(in_1), .out_6(l_4_bit_xor_1_out_6),
    .out_7(l_4_bit_xor_1_out_7), .out_8(l_4_bit_xor_1_out_8), .out_9(l_4_bit_xor_1_out_9));
  L_4_Bit_Xor l_4_bit_xor_2 (
    .in_2(in_3[8]), .in_3(in_3[9]), .in_4(in_3[10]), .in_5(in_3[11]), .in_1(in_1),
    .out_6(l_4_bit_xor_2_out_6), .out_7(l_4_bit_xor_2_out_7), .out_8(l_4_bit_xor_2_out_8),
    .out_9(l_4_bit_xor_2_out_9));
  L_4_Bit_Xor l_4_bit_xor_3 (
    .in_2(in_3[12]), .in_3(in_3[13]), .in_4(in_3[14]), .in_5(in_3[15]), .in_1(in_1),
    .out_6(l_4_bit_xor_3_out_6), .out_7(l_4_bit_xor_3_out_7), .out_8(l_4_bit_xor_3_out_8),
    .out_9(l_4_bit_xor_3_out_9));
  L_4b_ADD l_4b_add_1 (
    .B1(_7486_XOR_out_6), .A2(in_2[1]), .CIN(in_1), .B2(_7486_XOR_out_7), .A3(in_2[2]), .B3(_7486_XOR_out_8),
    .A4(in_2[3]), .B4(_7486_XOR_out_9), .A1(in_2[0]), .Y2(out_4[1]), .Y3(out_4[2]), .Y1(out_4[0]),
    .Y4(out_4[3]), .COUT(l_4b_add_1_cout));
  L_4b_ADD l_4b_add_2 (
    .B1(l_4_bit_xor_1_out_6), .A2(in_2[5]), .CIN(l_4b_add_1_cout), .B2(l_4_bit_xor_1_out_7), .A3(in_2[6]),
    .B3(l_4_bit_xor_1_out_8), .A4(in_2[7]), .B4(l_4_bit_xor_1_out_9), .A1(in_2[4]), .Y2(out_4[5]),
    .Y3(out_4[6]), .Y1(out_4[4]), .Y4(out_4[7]), .COUT(l_4b_add_2_cout));
  L_4b_ADD l_4b_add_3 (
    .B1(l_4_bit_xor_2_out_6), .A2(in_2[9]), .CIN(l_4b_add_2_cout), .B2(l_4_bit_xor_2_out_7), .A3(in_2[10]),
    .B3(l_4_bit_xor_2_out_8), .A4(in_2[11]), .B4(l_4_bit_xor_2_out_9), .A1(in_2[8]), .Y2(out_4[9]),
    .Y3(out_4[10]), .Y1(out_4[8]), .Y4(out_4[11]), .COUT(l_4b_add_3_cout));
  L_4b_ADD l_4b_add_4 (
    .B1(l_4_bit_xor_3_out_6), .A2(in_2[13]), .CIN(l_4b_add_3_cout), .B2(l_4_bit_xor_3_out_7), .A3(in_2[14]),
    .B3(l_4_bit_xor_3_out_8), .A4(in_2[15]), .B4(l_4_bit_xor_3_out_9), .A1(in_2[12]), .Y2(out_4[13]),
    .Y3(out_4[14]), .Y1(out_4[12]), .Y4(out_4[15]));  // open: COUT
endmodule

module L_4_Bit_Xor (
  input  in_1,
  input  in_2,
  input  in_3,
  input  in_4,
  input  in_5,
  output out_6,
  output out_7,
  output out_8,
  output out_9
);

  xor xor_1 (out_6, in_2, in_1);
  xor xor_2 (out_7, in_3, in_1);
  xor xor_3 (out_8, in_4, in_1);
  xor xor_4 (out_9, in_5, in_1);
endmodule

module L_16_Bit_Shifter_Right (
  input  in_1,
  input  [15:0] in_2,
  output [15:0] out_3
);

  wire dip_74157_1_p8;
  wire [14:0] dip_74157_1_p4;

  // DIP_74157 dip_74157_1: pin names not known; wires that end beside it: 1'b1, in_2[0], in_2[1], dip_74157_1_p4[0], in_2[1], in_2[2], dip_74157_1_p4[1], dip_74157_1_p8, in_2[3], in_2[4], dip_74157_1_p4[3], in_2[2], in_2[3], dip_74157_1_p4[2]
  // DIP_74157 dip_74157_2: pin names not known; wires that end beside it: 1'b1, in_2[4], in_2[5], dip_74157_1_p4[4], in_2[5], in_2[6], dip_74157_1_p4[5], dip_74157_1_p8, in_2[7], in_2[8], dip_74157_1_p4[7], in_2[6], in_2[7], dip_74157_1_p4[6]
  // DIP_74157 dip_74157_3: pin names not known; wires that end beside it: 1'b1, in_2[8], in_2[9], dip_74157_1_p4[8], in_2[9], in_2[10], dip_74157_1_p4[9], dip_74157_1_p8, in_2[11], in_2[12], dip_74157_1_p4[11], in_2[10], in_2[11], dip_74157_1_p4[10]
  // DIP_74157 dip_74157_4: pin names not known; wires that end beside it: 1'b1, in_2[12], in_2[13], dip_74157_1_p4[12], in_2[13], in_2[14], dip_74157_1_p4[13], dip_74157_1_p8, 1'b0, 1'b0, in_2[14], 1'b0, dip_74157_1_p4[14]
  not not_1 (dip_74157_1_p8, in_1);
  assign out_3 = in_1 ? {in_2[15], dip_74157_1_p4} : 16'bz;  // Controlled_Buffer controlled_buffer_1
endmodule

module ALU (
  input  in_1,
  input  in_2,
  input  [15:0] in_3,
  input  [15:0] in_4,
  output [15:0] out_5,
  output [15:0] out_6
);

  L_16_Bit_Adder l_16_bit_adder_1 (.in_1(in_1), .in_2(in_3), .in_3(in_4), .out_4(out_6));
  assign out_5 = in_2 ? out_6 : 16'bz;  // Controlled_Buffer controlled_buffer_1
  Multiplexer #(.select(3), .width(8)) multiplexer_1 ();  // open: in0, in1, in2, in3, in4, in5, in6, in7, out, sel
endmodule

module Ram_IO_MUX (
  input  in_1,
  input  in_2,
  input  [15:0] in_3,
  input  [15:0] in_4,
  output [15:0] out_5
);

  // IC_74157 ic_74157_1: pin names not known; wires that end beside it: in_3[0], in_4[0], in_3[1], in_4[1], in_3[2], in_4[2], in_1, out_5[0], out_5[1], out_5[2]
  // IC_74157 ic_74157_2: pin names not known; wires that end beside it: in_3[3], in_4[3], in_3[4], in_4[4], in_3[5], in_4[5], in_3[6], in_4[6], in_2, in_1, out_5[3], out_5[4], out_5[5], out_5[6]
  // IC_74157 ic_74157_3: pin names not known; wires that end beside it: in_3[7], in_4[7], in_3[8], in_4[8], in_3[9], in_4[9], in_3[10], in_4[10], in_2, in_1, out_5[7], out_5[8], out_5[9], out_5[10]
  // IC_74157 ic_74157_4: pin names not known; wires that end beside it: in_3[11], in_4[11], in_3[12], in_4[12], in_3[13], in_4[13], in_3[14], in_4[14], in_3[15], in_4[15], in_2, in_1, in_2, out_5[11], out_5[12], out_5[13], out_5[14], out_5[15]
endmodule

module MAR (
  input  in_1,
  input  [15:0] in_2,
  input  in_3,
  input  in_4,
  output [15:0] out_5
);

  C_74377 c_74377_1 (
    .CLR(in_4), .D2(in_2[1]), .D3(in_2[2]), .D1(in_2[0]), .D4(in_2[3]), .D5(in_2[4]), .D6(in_2[5]),
    .D7(in_2[6]), .D8(in_2[7]), .CLK(in_3), .EN(in_1), .Y2(out_5[1]), .Y3(out_5[2]), .Y1(out_5[0]),
    .Y4(out_5[3]), .Y5(out_5[4]), .Y6(out_5[5]), .Y7(out_5[6]), .Y8(out_5[7]));
  C_74377 c_74377_2 (
    .CLR(in_4), .D2(in_2[9]), .D3(in_2[10]), .D1(in_2[8]), .D4(in_2[11]), .D5(in_2[12]), .D6(in_2[13]),
    .D7(in_2[14]), .D8(in_2[15]), .CLK(in_3), .EN(in_1), .Y2(out_5[9]), .Y3(out_5[10]), .Y1(out_5[8]),
    .Y4(out_5[11]), .Y5(out_5[12]), .Y6(out_5[13]), .Y7(out_5[14]), .Y8(out_5[15]));
endmodule

module Ram_DATA_IO_MUX (
  input  in_1,
  input  in_2,
  input  [15:0] in_3,
  input  [15:0] in_4,
  output [15:0] out_5
);

  // IC_74157 ic_74157_1: pin names not known; wires that end beside it: in_3[0], in_4[0], in_3[1], in_4[1], in_3[2], in_4[2], in_1, out_5[0], out_5[1], out_5[2]
  // IC_74157 ic_74157_2: pin names not known; wires that end beside it: in_3[3], in_4[3], in_3[4], in_4[4], in_3[5], in_4[5], in_3[6], in_4[6], in_2, in_1, out_5[3], out_5[4], out_5[5], out_5[6]
  // IC_74157 ic_74157_3: pin names not known; wires that end beside it: in_3[7], in_4[7], in_3[8], in_4[8], in_3[9], in_4[9], in_3[10], in_4[10], in_2, in_1, out_5[7], out_5[8], out_5[9], out_5[10]
  // IC_74157 ic_74157_4: pin names not known; wires that end beside it: in_3[11], in_4[11], in_3[12], in_4[12], in_3[13], in_4[13], in_3[14], in_4[14], in_3[15], in_4[15], in_2, in_1, in_2, out_5[11], out_5[12], out_5[13], out_5[14], out_5[15]
endmodule

module testing (
  input  [15:0] in_1,
  input  in_2,
  input  [7:0] in_3,
  input  [7:0] in_4,
  output [7:0] out_5
);

  wire [3:0] rom_1_data, rom_1_data_2, rom_2_data, rom_2_data_2, rom_3_data, rom_3_data_2, rom_4_data,
       rom_4_data_2, rom_5_data, rom_5_data_2;

  Hex_Digit_Display hex_digit_display_1 (.value(rom_4_data_2));  // open: dp
  Hex_Digit_Display hex_digit_display_2 (.value(rom_2_data_2));  // open: dp
  Hex_Digit_Display hex_digit_display_3 (.value(rom_5_data_2));  // open: dp
  Hex_Digit_Display hex_digit_display_4 (.value(rom_3_data_2));  // open: dp
  Hex_Digit_Display hex_digit_display_5 (.value(rom_1_data_2));  // open: dp
  ROM #(.addrWidth(16)) rom_1 (.addr(in_1), .data({rom_1_data_2, rom_1_data}));
  ROM #(.addrWidth(16)) rom_2 (.addr(in_1), .data({rom_2_data_2, rom_2_data}));
  Hex_Digit_Display hex_digit_display_6 (.value(rom_4_data));  // open: dp
  Hex_Digit_Display hex_digit_display_7 (.value(rom_2_data));  // open: dp
  Hex_Digit_Display hex_digit_display_8 (.value(rom_5_data));  // open: dp
  Hex_Digit_Display hex_digit_display_9 (.value(rom_3_data));  // open: dp
  Hex_Digit_Display hex_digit_display_10 (.value(rom_1_data));  // open: dp
  ROM #(.addrWidth(16)) rom_3 (.addr(in_1), .data({rom_3_data_2, rom_3_data}));
  ROM #(.addrWidth(16)) rom_4 (.addr(in_1), .data({rom_4_data_2, rom_4_data}));
  ROM #(.addrWidth(16)) rom_5 (.addr(in_1), .data({rom_5_data_2, rom_5_data}));
  RAM #(.enables("line"), .\type ("nonvolatile")) ram_1 (.addr(in_3), .we(in_2), .clk(in_2), .din(in_4), .dout(out_5));

  // Notes on the sheet:
  //   contents of rom_1 (hex, n*v repeats v):
  //   0 11 22 33 44 55 66 77 88 99 0 11 22 33 44 55 66 77 88 99 0 11 22 33 44 55 66 77 88 99 0 11 22 33 44
  //   55 66 77 88 99 0 11 22 33 44 55 66 77 88 99 0 11 22 33 44 55 66 77 88 99 0 11 22 33 44 55 66 77 88
  //   99 0 11 22 33 44 55 66 77 88 99 0 11 22 33 44 55 66 77 88 99 0 11 22 33 44 55 66 77 88 99 0 11 22 33
  //   44 55 66 77 88 99 0 11 22 33 44 55 66 77 88 99 0 11 22 33 44 55 66 77 88 99 0 11 22 33 44 55 66 77
  //   88 99 0 11 22 33 44 55 66 77 88 99 0 11 22 33 44 55 66 77 88 99 0 11 22 33 44 55 66 77 88 99 0 11 22
  //   33 44 55 66 77 88 99 0 11 22 33 44 55 66 77 88 99 0 11 22 33 44 55 66 77 88 99 0 11 22 33 44 55 66
  //   77 88 99 0 11 22 33 44 55 66 77 88 99 0 11 22 33 44 55 66 77 88 99 0 11 22 33 44 55 66 77 88 99 0 11
  //   22 33 44 55 66 77 88 99 0 11 22 33 44 55 66 77 88 99 0 11 22 33 44 55 66 77 88 99 0 11 22 33 44 55
  //   66 77 88 99 0 11 22 33 44 55 66 77 88 99 0 11 22 33 44 55 66 77 88 99 0 11 22 33 44 55 66 77 88 99 0
  //   11 22 33 44 55 66 77 88 99 0 11 22 33 44 55 66 77 88 99 0 11 22 33 44 55 66 77 88 99 0 11 22 33 44
  //   55 66 77 88 99 0 11 22 33 44 55 66 77 88 99 0 11 22 33 44 55 66 77 88 99 0 11 22 33 44 55 66 77 88
  //   99 0 11 22 33 44 55 66 77 88 99 0 11 22 33 44 55 66 77 88 99 0 11 22 33 44 55 66 77 88 99 0 11 22 33
  //   44 55 66 77 88 99 0 11 22 33 44 55 66 77 88 99 0 11 22 33 44 55 66 77 88 99 0 11 22 33 44 55 66 77
  //   88 99 0 11 22 33 44 55 66 77 88 99 0 11 22 33 44 55 66 77 88 99 0 11 22 33 44 55 66 77 88 99 0 11 22
  //   33 44 55 66 77 88 99 0 11 22 33 44 55 66 77 88 99 0 11 22 33 44 55 66 77 88 99 0 11 22 33 44 55 66
  //   77 88 99 0 11 22 33 44 55 66 77 88 99 0 11 22 33 44 55 66 77 88 99 0 11 22 33 44 55 66 77 88 99 0 11
  //   22 33 44 55 66 77 88 99 0 11 22 33 44 55 66 77 88 99 0 11 22 33 44 55 66 77 88 99 0 11 22 33 44 55
  //   66 77 88 99 0 11 22 33 44 55 66 77 88 99 0 11 22 33 44 55 66 77 88 99 0 11 22 33 44 55 66 77 88 99 0
  //   11 22 33 44 55 66 77 88 99 0 11 22 33 44 55 66 77 88 99 0 11 22 33 44 55 66 77 88 99 0 11 22 33 44
  //   55 66 77 88 99 0 11 22 33 44 55 66 77 88 99 0 11 22 33 44 55 66 77 88 99 0 11 22 33 44 55 66 77 88
  //   99 0 11 22 33 44 55 66 77 88 99 0 11 22 33 44 55 66 77 88 99 0 11 22 33 44 55 66 77 88 99 0 11 22 33
  //   44 55 66 77 88 99 0 11 22 33 44 55 66 77 88 99 0 11 22 33 44 55 66 77 88 99 0 11 22 33 44 55 66 77
  //   88 99 0 11 22 33 44 55 66 77 88 99 0 11 22 33 44 55 66 77 88 99 0 11 22 33 44 55 66 77 88 99 0 11 22
  //   33 44 55 66 77 88 99 0 11 22 33 44 55 66 77 88 99 0 11 22 33 44 55 66 77 88 99 0 11 22 33 44 55 66
  //   77 88 99 0 11 22 33 44 55 66 77 88 99 0 11 22 33 44 55 66 77 88 99 0 11 22 33 44 55 66 77 88 99 0 11
  //   22 33 44 55 66 77 88 99 0 11 22 33 44 55 66 77 88 99 0 11 22 33 44 55 66 77 88 99 0 11 22 33 44 55
  //   66 77 88 99 0 11 22 33 44 55 66 77 88 99 0 11 22 33 44 55 66 77 88 99 0 11 22 33 44 55 66 77 88 99 0
  //   11 22 33 44 55 66 77 88 99 0 11 22 33 44 55 66 77 88 99 0 11 22 33 44 55 66 77 88 99 0 11 22 33 44
  //   55 66 77 88 99 0 11 22 33 44 55 66 77 88 99 0 11 22 33 44 55 66 77 88 99 0 11 22 33 44 55 66 77 88
  //   99 0 11 22 33 44 55 66 77 88 99 0 11 22 33 44 55 66 77 88 99 0 11 22 33 44 55 66 77 88 99 0 11 22 33
  //   44 55 66 77 88 99 0 11 22 33 44 55 66 77 88 99 0 11 22 33 44 55 66 77 88 99 0 11 22 33 44 55 66 77
  //   88 99 0 11 22 33 44 55 66 77 88 99 0 11 22 33 44 55 66 77 88 99 0 11 22 33 44 55 66 77 88 99 0 11 22
  //   33 44 55 66 77 88 99 0 11 22 33 44 55 66 77 88 99 0 11 22 33 44 55 66 77 88 99 0 11 22 33 44 55 66
  //   77 88 99 0 11 22 33 44 55 66 77 88 99 0 11 22 33 44 55 66 77 88 99 0 11 22 33 44 55 66 77 88 99 0 11
  //   22 33 44 55 66 77 88 99 0 11 22 33 44 55 66 77 88 99 0 11 22 33 44 55 66 77 88 99 0 11 22 33 44 55
  //   66 77 88 99 0 11 22 33 44 55 66 77 88 99 0 11 22 33 44 55 66 77 88 99 0 11 22 33 44 55 66 77 88 99 0
  //   11 22 33 44 55 66 77 88 99 0 11 22 33 44 55 66 77 88 99 0 11 22 33 44 55 66 77 88 99 0 11 22 33 44
  //   55 66 77 88 99 0 11 22 33 44 55 66 77 88 99 0 11 22 33 44 55 66 77 88 99 0 11 22 33 44 55 66 77 88
  //   99 0 11 22 33 44 55 66 77 88 99 0 11 22 33 44 55 66 77 88 99 0 11 22 33 44 55 66 77 88 99 0 11 22 33
  //   44 55 66 77 88 99 0 11 22 33 44 55 66 77 88 99 0 11 22 33 44 55 66 77 88 99 0 11 22 33 44 55 66 77
  //   88 9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
  //   contents of rom_2 (hex, n*v repeats v):
  //   1000*0 1000*11 1000*22 1000*33 1000*44 1000*55 1000*66 1000*77 1000*88 1000*99 1000*0 1000*11
  //   1000*22 1000*33 1000*44 1000*55 1000*66 1000*77 1000*88 1000*99 1000*0 1000*11 1000*22 1000*33
  //   1000*44 1000*55 1000*66 1000*77 1000*88 1000*99 1000*0 1000*11 1000*22 537*32 463*31 537*41 463*40
  //   537*50 463*59 537*69 463*68 537*78 463*77 537*87 463*86 537*96 463*95 537*5 463*4 537*14 463*13
  //   537*23 463*22 537*32 463*31 537*41 463*40 537*50 463*59 537*69 463*68 537*78 463*77 537*87 463*86
  //   537*96 463*95 537*5 463*4 537*14 463*13 537*23 463*22 537*32 463*31 537*41 463*40 537*50 463*59
  //   537*69 463*68 537*78 463*77 537*87 463*86 537*96 463*95 537*5 463*4 537*14 463*13 537*23 463*22
  //   537*32 463*31 537*41 463*40 536*50
  //   contents of rom_3 (hex, n*v repeats v):
  //   10*0 10*11 10*22 10*33 10*44 10*55 10*66 10*77 10*88 10*99 10*0 10*11 10*22 10*33 10*44 10*55 10*66
  //   10*77 10*88 10*99 10*0 10*11 10*22 10*33 10*44 10*55 10*66 10*77 10*88 10*99 10*0 10*11 10*22 10*33
  //   10*44 10*55 10*66 10*77 10*88 10*99 10*0 10*11 10*22 10*33 10*44 10*55 10*66 10*77 10*88 10*99 10*0
  //   10*11 10*22 10*33 10*44 10*55 10*66 10*77 10*88 10*99 10*0 10*11 10*22 10*33 10*44 10*55 10*66 10*77
  //   10*88 10*99 10*0 10*11 10*22 10*33 10*44 10*55 10*66 10*77 10*88 10*99 10*0 10*11 10*22 10*33 10*44
  //   10*55 10*66 10*77 10*88 10*99 10*0 10*11 10*22 10*33 10*44 10*55 10*66 10*77 10*88 10*99 10*0 10*11
  //   10*22 10*33 10*44 10*55 10*66 10*77 10*88 10*99 10*0 10*11 10*22 10*33 10*44 10*55 10*66 10*77 10*88
  //   10*99 10*0 10*11 10*22 10*33 10*44 10*55 10*66 10*77 10*88 10*99 10*0 10*11 10*22 10*33 10*44 10*55
  //   10*66 10*77 10*88 10*99 10*0 10*11 10*22 10*33 10*44 10*55 10*66 10*77 10*88 10*99 10*0 10*11 10*22
  //   10*33 10*44 10*55 10*66 10*77 10*88 10*99 10*0 10*11 10*22 10*33 10*44 10*55 10*66 10*77 10*88 10*99
  //   10*0 10*11 10*22 10*33 10*44 10*55 10*66 10*77 10*88 10*99 10*0 10*11 10*22 10*33 10*44 10*55 10*66
  //   10*77 10*88 10*99 10*0 10*11 10*22 10*33 10*44 10*55 10*66 10*77 10*88 10*99 10*0 10*11 10*22 10*33
  //   10*44 10*55 10*66 10*77 10*88 10*99 10*0 10*11 10*22 10*33 10*44 10*55 10*66 10*77 10*88 10*99 10*0
  //   10*11 10*22 10*33 10*44 10*55 10*66 10*77 10*88 10*99 10*0 10*11 10*22 10*33 10*44 10*55 10*66 10*77
  //   10*88 10*99 10*0 10*11 10*22 10*33 10*44 10*55 10*66 10*77 10*88 10*99 10*0 10*11 10*22 10*33 10*44
  //   10*55 10*66 10*77 10*88 10*99 10*0 10*11 10*22 10*33 10*44 10*55 10*66 10*77 10*88 10*99 10*0 10*11
  //   10*22 10*33 10*44 10*55 10*66 10*77 10*88 10*99 10*0 10*11 10*22 10*33 10*44 10*55 10*66 10*77 10*88
  //   10*99 10*0 10*11 10*22 10*33 10*44 10*55 10*66 10*77 10*88 10*99 10*0 10*11 10*22 10*33 10*44 10*55
  //   10*66 10*77 10*88 10*99 10*0 10*11 10*22 10*33 10*44 10*55 10*66 10*77 10*88 10*99 10*0 10*11 10*22
  //   10*33 10*44 10*55 10*66 10*77 10*88 10*99 10*0 10*11 10*22 10*33 10*44 10*55 10*66 10*77 10*88 10*99
  //   10*0 10*11 10*22 10*33 10*44 10*55 10*66 10*77 10*88 10*99 10*0 10*11 10*22 10*33 10*44 10*55 10*66
  //   10*77 10*88 10*99 10*0 10*11 10*22 10*33 10*44 10*55 10*66 10*77 10*88 10*99 10*0 10*11 10*22 10*33
  //   10*44 10*55 10*66 10*77 10*88 10*99 10*0 10*11 10*22 10*33 10*44 10*55 10*66 10*77 10*88 10*99 10*0
  //   10*11 10*22 10*33 10*44 10*55 10*66 10*77 10*88 10*99 10*0 10*11 10*22 10*33 10*44 10*55 10*66 10*77
  //   10*88 10*99 10*0 10*11 10*22 10*33 10*44 10*55 10*66 10*77 10*88 10*99 10*0 10*11 10*22 10*33 10*44
  //   10*55 10*66 10*77 10*88 10*99 10*0 10*11 10*22 10*33 10*44 10*55 10*66 10*77 10*88 10*99 10*0 10*11
  //   10*22 10*33 10*44 10*55 10*66 10*77 10*88 10*99 10*0 10*11 10*22 10*33 10*44 10*55 10*66 10*77 10*88
  //   10*99 10*0 10*11 10*22 10*33 10*44 10*55 10*66 10*77 10*88 10*99 10*0 10*11 10*22 10*33 10*44 10*55
  //   10*66 10*77 10*88 10*99 10*0 10*11 10*22 10*33 10*44 10*55 10*66 10*77 10*88 10*99 10*0 10*11 10*22
  //   10*33 10*44 10*55 10*66 10*77 10*88 10*99 10*0 10*11 10*22 10*33 10*44 10*55 10*66 10*77 10*88 10*99
  //   10*0 10*11 10*22 10*33 10*44 10*55 10*66 10*77 10*88 10*99 10*0 10*11 10*22 10*33 10*44 10*55 10*66
  //   10*77 10*88 10*99 10*0 10*11 10*22 10*33 10*44 10*55 10*66 10*77 10*88 10*99 10*0 10*11 10*22 10*33
  //   10*44 10*55 10*66 10*77 10*88 10*99 10*0 10*11 10*22 10*33 10*44 10*55 10*66 10*77 10*88 10*99 10*0
  //   10*11 10*22 10*33 10*44 10*55 10*66 10*77 10*88 10*99 10*0 10*11 10*22 10*33 10*44 10*55 10*66 10*77
  //   10*88 10*99 10*0 10*11 10*22 10*33 10*44 10*55 10*66 10*77 10*88 10*99 10*0 10*11 10*22 10*33 10*44
  //   10*55 10*66 10*77 10*88 10*99 10*0 10*11 10*22 10*33 10*44 10*55 10*66 10*77 10*88 10*99 10*0 10*11
  //   10*22 10*33 10*44 10*55 10*66 10*77 10*88 10*99 10*0 10*11 10*22 10*33 10*44 10*55 10*66 10*77 10*88
  //   10*99 10*0 10*11 10*22 10*33 10*44 10*55 10*66 10*77 10*88 10*99 10*0 10*11 10*22 10*33 10*44 10*55
  //   10*66 10*77 10*88 10*99 10*0 10*11 10*22 10*33 10*44 10*55 10*66 10*77 10*88 10*99 10*0 10*11 10*22
  //   10*33 10*44 10*55 10*66 10*77 10*88 10*99 10*0 10*11 10*22 10*33 10*44 10*55 10*66 10*77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
  //   contents of rom_4 (hex, n*v repeats v):
  //   10000*0 10000*11 10000*22 5537*33 4463*32 5537*42 4463*41 5537*51 4463*50 5536*60
  //   contents of rom_5 (hex, n*v repeats v):
  //   100*0 100*11 100*22 100*33 100*44 100*55 100*66 100*77 100*88 100*99 100*0 100*11 100*22 100*33
  //   100*44 100*55 100*66 100*77 100*88 100*99 100*0 100*11 100*22 100*33 100*44 100*55 100*66 100*77
  //   100*88 100*99 100*0 100*11 100*22 100*33 100*44 100*55 100*66 100*77 100*88 100*99 100*0 100*11
  //   100*22 100*33 100*44 100*55 100*66 100*77 100*88 100*99 100*0 100*11 100*22 100*33 100*44 100*55
  //   100*66 100*77 100*88 100*99 100*0 100*11 100*22 100*33 100*44 100*55 100*66 100*77 100*88 100*99
  //   100*0 100*11 100*22 100*33 100*44 100*55 100*66 100*77 100*88 100*99 100*0 100*11 100*22 100*33
  //   100*44 100*55 100*66 100*77 100*88 100*99 100*0 100*11 100*22 100*33 100*44 100*55 100*66 100*77
  //   100*88 100*99 100*0 100*11 100*22 100*33 100*44 100*55 100*66 100*77 100*88 100*99 100*0 100*11
  //   100*22 100*33 100*44 100*55 100*66 100*77 100*88 100*99 100*0 100*11 100*22 100*33 100*44 100*55
  //   100*66 100*77 100*88 100*99 100*0 100*11 100*22 100*33 100*44 100*55 100*66 100*77 100*88 100*99
  //   100*0 100*11 100*22 100*33 100*44 100*55 100*66 100*77 100*88 100*99 100*0 100*11 100*22 100*33
  //   100*44 100*55 100*66 100*77 100*88 100*99 100*0 100*11 100*22 100*33 100*44 100*55 100*66 100*77
  //   100*88 100*99 100*0 100*11 100*22 100*33 100*44 100*55 100*66 100*77 100*88 100*99 100*0 100*11
  //   100*22 100*33 100*44 100*55 100*66 100*77 100*88 100*99 100*0 100*11 100*22 100*33 100*44 100*55
  //   100*66 100*77 100*88 100*99 100*0 100*11 100*22 100*33 100*44 100*55 100*66 100*77 100*88 100*99
  //   100*0 100*11 100*22 100*33 100*44 100*55 100*66 100*77 100*88 100*99 100*0 100*11 100*22 100*33
  //   100*44 100*55 100*66 100*77 100*88 100*99 100*0 100*11 100*22 100*33 100*44 100*55 100*66 100*77
  //   100*88 100*99 100*0 100*11 100*22 100*33 100*44 100*55 100*66 100*77 100*88 100*99 100*0 100*11
  //   100*22 100*33 100*44 100*55 100*66 100*77 100*88 100*99 100*0 100*11 100*22 100*33 100*44 100*55
  //   100*66 100*77 100*88 100*99 100*0 100*11 100*22 100*33 100*44 100*55 100*66 100*77 100*88 100*99
  //   100*0 100*11 100*22 100*33 100*44 100*55 100*66 100*77 100*88 100*99 100*0 100*11 100*22 100*33
  //   100*44 100*55 100*66 100*77 100*88 100*99 100*0 100*11 100*22 100*33 100*44 100*55 100*66 100*77
  //   100*88 100*99 100*0 100*11 100*22 100*33 100*44 100*55 100*66 100*77 100*88 100*99 100*0 100*11
  //   100*22 100*33 100*44 100*55 100*66 100*77 37*87 63*86 37*96 63*95 37*5 63*4 37*14 63*13 37*23 63*22
  //   37*32 63*31 37*41 63*40 37*50 63*59 37*69 63*68 37*78 63*77 37*87 63*86 37*96 63*95 37*5 63*4 37*14
  //   63*13 37*23 63*22 37*32 63*31 37*41 63*40 37*50 63*59 37*69 63*68 37*78 63*77 37*87 63*86 37*96
  //   63*95 37*5 63*4 37*14 63*13 37*23 63*22 37*32 63*31 37*41 63*40 37*50 63*59 37*69 63*68 37*78 63*77
  //   37*87 63*86 37*96 63*95 37*5 63*4 37*14 63*13 37*23 63*22 37*32 63*31 37*41 63*40 37*50 63*59 37*69
  //   63*68 37*78 63*77 37*87 63*86 37*96 63*95 37*5 63*4 37*14 63*13 37*23 63*22 37*32 63*31 37*41 63*40
  //   37*50 63*59 37*69 63*68 37*78 63*77 37*87 63*86 37*96 63*95 37*5 63*4 37*14 63*13 37*23 63*22 37*32
  //   63*31 37*41 63*40 37*50 63*59 37*69 63*68 37*78 63*77 37*87 63*86 37*96 63*95 37*5 63*4 37*14 63*13
  //   37*23 63*22 37*32 63*31 37*41 63*40 37*50 63*59 37*69 63*68 37*78 63*77 37*87 63*86 37*96 63*95 37*5
  //   63*4 37*14 63*13 37*23 63*22 37*32 63*31 37*41 63*40 37*50 63*59 37*69 63*68 37*78 63*77 37*87 63*86
  //   37*96 63*95 37*5 63*4 37*14 63*13 37*23 63*22 37*32 63*31 37*41 63*40 37*50 63*59 37*69 63*68 37*78
  //   63*77 37*87 63*86 37*96 63*95 37*5 63*4 37*14 63*13 37*23 63*22 37*32 63*31 37*41 63*40 37*50 63*59
  //   37*69 63*68 37*78 63*77 37*87 63*86 37*96 63*95 37*5 63*4 37*14 63*13 37*23 63*22 37*32 63*31 37*41
  //   63*40 37*50 63*59 37*69 63*68 37*78 63*77 37*87 63*86 37*96 63*95 37*5 63*4 37*14 63*13 37*23 63*22
  //   37*32 63*31 37*41 63*40 37*50 63*59 37*69 63*68 37*78 63*77 37*87 63*86 37*96 63*95 37*5 63*4 37*14
  //   63*13 37*23 63*22 37*32 63*31 37*41 63*40 37*50 63*59 37*69 63*68 37*78 63*77 37*87 63*86 37*96
  //   63*95 37*5 63*4 37*14 63*13 37*23 63*22 37*32 63*31 37*41 63*40 37*50 63*59 37*69 63*68 37*78 63*77
  //   37*87 63*86 37*96 63*95 37*5 63*4 37*14 63*13 37*23 63*22 37*32 63*31 37*41 63*40 37*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
endmodule

module ROM_DIS (
  input  in_1,
  input  [15:0] in_2,
  output out_3,
  output [3:0] out_4,
  output [3:0] out_5,
  output [3:0] out_6,
  output [3:0] out_7,
  output [3:0] out_8
);

  wire [3:0] HUNS_data, HUNS_data_2, ONES_data, ONES_data_2, TENS_data, TENS_data_2, THOU_data, THOU_data_2,
       TTHOU_data, TTHOU_data_2;

  and and_1 (out_3, in_1, in_2[15]);
  Multiplexer #(.width(4)) multiplexer_1 (.in0(TTHOU_data_2), .in1(TTHOU_data), .out(out_4), .sel(in_1));
  ROM #(.addrWidth(16)) ONES (.addr(in_2), .data({ONES_data_2, ONES_data}));
  ROM #(.addrWidth(16)) THOU (.addr(in_2), .data({THOU_data_2, THOU_data}));
  Multiplexer #(.width(4)) multiplexer_2 (.in0(THOU_data_2), .in1(THOU_data), .out(out_5), .sel(in_1));
  Multiplexer #(.width(4)) multiplexer_3 (.in0(HUNS_data_2), .in1(HUNS_data), .out(out_6), .sel(in_1));
  Multiplexer #(.width(4)) multiplexer_4 (.in0(TENS_data_2), .in1(TENS_data), .out(out_7), .sel(in_1));
  Multiplexer #(.width(4)) multiplexer_5 (.in0(ONES_data_2), .in1(ONES_data), .out(out_8), .sel(in_1));
  ROM #(.addrWidth(16)) TENS (.addr(in_2), .data({TENS_data_2, TENS_data}));
  ROM #(.addrWidth(16)) TTHOU (.addr(in_2), .data({TTHOU_data_2, TTHOU_data}));
  ROM #(.addrWidth(16)) HUNS (.addr(in_2), .data({HUNS_data_2, HUNS_data}));

  // Notes on the sheet:
  //   contents of ONES (hex, n*v repeats v):
  //   0 11 22 33 44 55 66 77 88 99 0 11 22 33 44 55 66 77 88 99 0 11 22 33 44 55 66 77 88 99 0 11 22 33 44
  //   55 66 77 88 99 0 11 22 33 44 55 66 77 88 99 0 11 22 33 44 55 66 77 88 99 0 11 22 33 44 55 66 77 88
  //   99 0 11 22 33 44 55 66 77 88 99 0 11 22 33 44 55 66 77 88 99 0 11 22 33 44 55 66 77 88 99 0 11 22 33
  //   44 55 66 77 88 99 0 11 22 33 44 55 66 77 88 99 0 11 22 33 44 55 66 77 88 99 0 11 22 33 44 55 66 77
  //   88 99 0 11 22 33 44 55 66 77 88 99 0 11 22 33 44 55 66 77 88 99 0 11 22 33 44 55 66 77 88 99 0 11 22
  //   33 44 55 66 77 88 99 0 11 22 33 44 55 66 77 88 99 0 11 22 33 44 55 66 77 88 99 0 11 22 33 44 55 66
  //   77 88 99 0 11 22 33 44 55 66 77 88 99 0 11 22 33 44 55 66 77 88 99 0 11 22 33 44 55 66 77 88 99 0 11
  //   22 33 44 55 66 77 88 99 0 11 22 33 44 55 66 77 88 99 0 11 22 33 44 55 66 77 88 99 0 11 22 33 44 55
  //   66 77 88 99 0 11 22 33 44 55 66 77 88 99 0 11 22 33 44 55 66 77 88 99 0 11 22 33 44 55 66 77 88 99 0
  //   11 22 33 44 55 66 77 88 99 0 11 22 33 44 55 66 77 88 99 0 11 22 33 44 55 66 77 88 99 0 11 22 33 44
  //   55 66 77 88 99 0 11 22 33 44 55 66 77 88 99 0 11 22 33 44 55 66 77 88 99 0 11 22 33 44 55 66 77 88
  //   99 0 11 22 33 44 55 66 77 88 99 0 11 22 33 44 55 66 77 88 99 0 11 22 33 44 55 66 77 88 99 0 11 22 33
  //   44 55 66 77 88 99 0 11 22 33 44 55 66 77 88 99 0 11 22 33 44 55 66 77 88 99 0 11 22 33 44 55 66 77
  //   88 99 0 11 22 33 44 55 66 77 88 99 0 11 22 33 44 55 66 77 88 99 0 11 22 33 44 55 66 77 88 99 0 11 22
  //   33 44 55 66 77 88 99 0 11 22 33 44 55 66 77 88 99 0 11 22 33 44 55 66 77 88 99 0 11 22 33 44 55 66
  //   77 88 99 0 11 22 33 44 55 66 77 88 99 0 11 22 33 44 55 66 77 88 99 0 11 22 33 44 55 66 77 88 99 0 11
  //   22 33 44 55 66 77 88 99 0 11 22 33 44 55 66 77 88 99 0 11 22 33 44 55 66 77 88 99 0 11 22 33 44 55
  //   66 77 88 99 0 11 22 33 44 55 66 77 88 99 0 11 22 33 44 55 66 77 88 99 0 11 22 33 44 55 66 77 88 99 0
  //   11 22 33 44 55 66 77 88 99 0 11 22 33 44 55 66 77 88 99 0 11 22 33 44 55 66 77 88 99 0 11 22 33 44
  //   55 66 77 88 99 0 11 22 33 44 55 66 77 88 99 0 11 22 33 44 55 66 77 88 99 0 11 22 33 44 55 66 77 88
  //   99 0 11 22 33 44 55 66 77 88 99 0 11 22 33 44 55 66 77 88 99 0 11 22 33 44 55 66 77 88 99 0 11 22 33
  //   44 55 66 77 88 99 0 11 22 33 44 55 66 77 88 99 0 11 22 33 44 55 66 77 88 99 0 11 22 33 44 55 66 77
  //   88 99 0 11 22 33 44 55 66 77 88 99 0 11 22 33 44 55 66 77 88 99 0 11 22 33 44 55 66 77 88 99 0 11 22
  //   33 44 55 66 77 88 99 0 11 22 33 44 55 66 77 88 99 0 11 22 33 44 55 66 77 88 99 0 11 22 33 44 55 66
  //   77 88 99 0 11 22 33 44 55 66 77 88 99 0 11 22 33 44 55 66 77 88 99 0 11 22 33 44 55 66 77 88 99 0 11
  //   22 33 44 55 66 77 88 99 0 11 22 33 44 55 66 77 88 99 0 11 22 33 44 55 66 77 88 99 0 11 22 33 44 55
  //   66 77 88 99 0 11 22 33 44 55 66 77 88 99 0 11 22 33 44 55 66 77 88 99 0 11 22 33 44 55 66 77 88 99 0
  //   11 22 33 44 55 66 77 88 99 0 11 22 33 44 55 66 77 88 99 0 11 22 33 44 55 66 77 88 99 0 11 22 33 44
  //   55 66 77 88 99 0 11 22 33 44 55 66 77 88 99 0 11 22 33 44 55 66 77 88 99 0 11 22 33 44 55 66 77 88
  //   99 0 11 22 33 44 55 66 77 88 99 0 11 22 33 44 55 66 77 88 99 0 11 22 33 44 55 66 77 88 99 0 11 22 33
  //   44 55 66 77 88 99 0 11 22 33 44 55 66 77 88 99 0 11 22 33 44 55 66 77 88 99 0 11 22 33 44 55 66 77
  //   88 99 0 11 22 33 44 55 66 77 88 99 0 11 22 33 44 55 66 77 88 99 0 11 22 33 44 55 66 77 88 99 0 11 22
  //   33 44 55 66 7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
  //   contents of THOU (hex, n*v repeats v):
  //   1000*0 1000*11 1000*22 1000*33 1000*44 1000*55 1000*66 1000*77 1000*88 1000*99 1000*0 1000*11
  //   1000*22 1000*33 1000*44 1000*55 1000*66 1000*77 1000*88 1000*99 1000*0 1000*11 1000*22 1000*33
  //   1000*44 1000*55 1000*66 1000*77 1000*88 1000*99 1000*0 1000*11 1000*22 537*32 463*31 537*41 463*40
  //   537*50 463*5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
  //   contents of TENS (hex, n*v repeats v):
  //   10*0 10*11 10*22 10*33 10*44 10*55 10*66 10*77 10*88 10*99 10*0 10*11 10*22 10*33 10*44 10*55 10*66
  //   10*77 10*88 10*99 10*0 10*11 10*22 10*33 10*44 10*55 10*66 10*77 10*88 10*99 10*0 10*11 10*22 10*33
  //   10*44 10*55 10*66 10*77 10*88 10*99 10*0 10*11 10*22 10*33 10*44 10*55 10*66 10*77 10*88 10*99 10*0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
  //   contents of TTHOU (hex, n*v repeats v):
  //   10000*0 10000*11 10000*22 5537*33 4463*32 5537*42 4463*41 5537*51 4463*50 5536*60
  //   contents of HUNS (hex, n*v repeats v):
  //   100*0 100*11 100*22 100*33 100*44 100*55 100*66 100*77 100*88 100*99 100*0 100*11 100*22 100*33
  //   100*44 100*55 100*66 100*77 100*88 100*99 100*0 100*11 100*22 100*33 100*44 100*55 100*66 100*77
  //   100*88 100*99 100*0 100*11 100*22 100*33 100*44 100*55 100*66 100*77 100*88 100*99 100*0 100*11
  //   100*22 100*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
endmodule

module OUT_REG (
  input  in_1,
  input  in_2,
  input  [15:0] in_3,
  output [15:0] out_4
);

  C_74173 c_74173_1 (
    .D2(in_3[1]), .D3(in_3[2]), .D1(in_3[0]), .D4(in_3[3]), .CLK(in_2), .CE1(in_1), .CE2(in_1), .OE1(1'b0),
    .OE2(1'b0), .Q2(out_4[1]), .Q3(out_4[2]), .Q1(out_4[0]), .Q4(out_4[3]));  // open: CLR
  C_74173 c_74173_2 (
    .D2(in_3[5]), .D3(in_3[6]), .D1(in_3[4]), .D4(in_3[7]), .CLK(in_2), .CE1(in_1), .CE2(in_1), .OE1(1'b0),
    .OE2(1'b0), .Q2(out_4[5]), .Q3(out_4[6]), .Q1(out_4[4]), .Q4(out_4[7]));  // open: CLR
  C_74173 c_74173_3 (
    .D2(in_3[9]), .D3(in_3[10]), .D1(in_3[8]), .D4(in_3[11]), .CLK(in_2), .CE1(in_1), .CE2(in_1), .OE1(1'b0),
    .OE2(1'b0), .Q2(out_4[9]), .Q3(out_4[10]), .Q1(out_4[8]), .Q4(out_4[11]));  // open: CLR
  C_74173 c_74173_4 (
    .D2(in_3[13]), .D3(in_3[14]), .D1(in_3[12]), .D4(in_3[15]), .CLK(in_2), .CE1(in_1), .CE2(in_1),
    .OE1(1'b0), .OE2(1'b0), .Q2(out_4[13]), .Q3(out_4[14]), .Q1(out_4[12]), .Q4(out_4[15]));  // open: CLR
endmodule

module Instruction_Register (
  input  in_1,
  input  in_2,
  input  in_3,
  input  in_4,
  input  [7:0] in_5,
  output [3:0] out_6,
  output [7:0] out_7,
  output [3:0] out_8
);

  C_74173 c_74173_1 (
    .D2(in_5[1]), .D3(in_5[2]), .D1(in_5[0]), .D4(in_5[3]), .CLK(in_3), .CE1(in_2), .CE2(in_2), .CLR(in_1),
    .OE1(1'b0), .OE2(1'b0), .Q2(out_7[1]), .Q3(out_7[2]), .Q1(out_7[0]), .Q4(out_7[3]));
  C_74173 c_74173_2 (
    .D2(in_5[5]), .D3(in_5[6]), .D1(in_5[4]), .D4(in_5[7]), .CLK(in_3), .CE1(in_2), .CE2(in_2), .CLR(in_1),
    .OE1(1'b0), .OE2(1'b0), .Q2(out_7[5]), .Q3(out_7[6]), .Q1(out_7[4]), .Q4(out_7[7]));
  assign out_6 = in_4 ? out_7[3:0] : 4'bz;  // Controlled_Buffer controlled_buffer_1

  assign out_8 = out_7[7:4];

  // Notes on the sheet:
  //   IAR
  //   IR
endmodule

module C_74161 (
  input  CLK,
  input  CLR,
  input  LE,
  input  CEP,
  input  CET,
  input  D1,
  input  D2,
  input  D3,
  input  D4,
  output Q1,
  output Q2,
  output Q3,
  output Q4,
  output TC
);

  wire and_1_out, and_2_out, and_3_out, and_4_out, and_5_out, and_6_out, and_7_out, and_8_out, and_9_out,
       and_10_out, and_11_out, and_12_out, not_1_out, not_2_out, not_3_out, or_1_out, or_2_out, or_3_out,
       or_4_out, xor_1_out, xor_2_out, xor_3_out, xor_4_out;

  not not_1 (not_1_out, CLK);
  not not_2 (not_2_out, CLR);
  and and_1 (and_1_out, LE, CEP, CET);
  not not_3 (not_3_out, LE);
  and and_2 (and_2_out, D1, not_3_out);
  and and_3 (and_3_out, Q1, LE);
  and and_4 (and_4_out, D2, not_3_out);
  and and_5 (and_5_out, Q2, LE);
  and and_6 (and_6_out, Q1, and_1_out);
  and and_7 (and_7_out, D3, not_3_out);
  and and_8 (and_8_out, Q3, LE);
  and and_9 (and_9_out, Q2, Q1, and_1_out);
  and and_10 (and_10_out, D4, not_3_out);
  and and_11 (and_11_out, Q4, LE);
  and and_12 (and_12_out, Q3, Q2, Q1, and_1_out);
  xor xor_1 (xor_1_out, and_3_out, and_1_out);
  xor xor_2 (xor_2_out, and_5_out, and_6_out);
  xor xor_3 (xor_3_out, and_8_out, and_9_out);
  xor xor_4 (xor_4_out, and_11_out, and_12_out);
  or or_1 (or_1_out, and_2_out, xor_1_out);
  or or_2 (or_2_out, and_4_out, xor_2_out);
  or or_3 (or_3_out, and_7_out, xor_3_out);
  or or_4 (or_4_out, and_10_out, xor_4_out);
  D_Flip_Flop d_ff_1 (.D(or_1_out), .clk(not_1_out), .Q(Q1), .reset(not_2_out));  // open: Qn, preset
  D_Flip_Flop d_ff_2 (.D(or_2_out), .clk(not_1_out), .Q(Q2), .reset(not_2_out));  // open: Qn, preset
  D_Flip_Flop d_ff_3 (.D(or_3_out), .clk(not_1_out), .Q(Q3), .reset(not_2_out));  // open: Qn, preset
  D_Flip_Flop d_ff_4 (.D(or_4_out), .clk(not_1_out), .Q(Q4), .reset(not_2_out));  // open: Qn, preset
  and and_13 (TC, Q4, Q3, Q2, Q1, CET);
endmodule

module C_74173 (
  input  D1,
  input  D2,
  input  D3,
  input  D4,
  input  CLK,
  input  CE1,
  input  CE2,
  input  CLR,
  input  OE1,
  input  OE2,
  output Q1,
  output Q2,
  output Q3,
  output Q4
);

  wire and_1_out, d_ff_1_q, d_ff_2_q, d_ff_3_q, d_ff_4_q, nor_1_out, nor_2_out;

  nor nor_1 (nor_1_out, CE1, CE2);
  nor nor_2 (nor_2_out, OE1, OE2);
  and and_1 (and_1_out, CLK, nor_1_out);
  D_Flip_Flop d_ff_1 (.D(D1), .clk(and_1_out), .Q(d_ff_1_q), .reset(CLR));  // open: Qn, preset
  D_Flip_Flop d_ff_2 (.D(D2), .clk(and_1_out), .Q(d_ff_2_q), .reset(CLR));  // open: Qn, preset
  D_Flip_Flop d_ff_3 (.D(D3), .clk(and_1_out), .Q(d_ff_3_q), .reset(CLR));  // open: Qn, preset
  D_Flip_Flop d_ff_4 (.D(D4), .clk(and_1_out), .Q(d_ff_4_q), .reset(CLR));  // open: Qn, preset
  assign Q1 = nor_2_out ? d_ff_1_q : 1'bz;  // Controlled_Buffer controlled_buffer_1
  assign Q2 = nor_2_out ? d_ff_2_q : 1'bz;  // Controlled_Buffer controlled_buffer_2
  assign Q3 = nor_2_out ? d_ff_3_q : 1'bz;  // Controlled_Buffer controlled_buffer_3
  assign Q4 = nor_2_out ? d_ff_4_q : 1'bz;  // Controlled_Buffer controlled_buffer_4
endmodule

module Control_unit (
  input  [3:0] INSTRUCTION,
  input  CLK,
  output [7:0] STEP,
  output HLT,
  output MAR_I,
  output RAM_I,
  output RAM_O,
  output IR_0,
  output IR_I,
  output A_I,
  output A_O,
  output ALU_O,
  output SUB,
  output B_I,
  output O_I,
  output CE,
  output C0,
  output JUMP,
  output B_O
);

  wire c_74161_1_q4;
  wire [2:0] c_74161_1_q1;

  C_74161 c_74161_1 (
    .CLK(CLK), .CLR(1'b1), .LE(1'b1), .CEP(1'b1), .CET(1'b1), .Q1(c_74161_1_q1[0]), .Q2(c_74161_1_q1[1]),
    .Q3(c_74161_1_q1[2]), .Q4(c_74161_1_q4));  // open: D1, D2, D3, D4, TC
  // IC_74138 ic_74138_1: pin names not known; wires that end beside it: c_74161_1_q4, c_74161_1_q1[0], c_74161_1_q1[1], c_74161_1_q1[2], 1'b0, 1'b0, 1'b1, STEP[0], STEP[1], STEP[2], STEP[3], STEP[4], STEP[5], STEP[6], STEP[7]
  ROM #(.addrWidth(11)) rom_1 (
    .addr({3'b000, INSTRUCTION, 1'b0, c_74161_1_q1}), .data({HLT, MAR_I, RAM_I, RAM_O, IR_0, IR_I, A_I, A_O}));
  ROM #(.addrWidth(11)) rom_2 (
    .addr({3'b000, INSTRUCTION, 1'b0, c_74161_1_q1}), .data({ALU_O, SUB, B_I, O_I, CE, C0, JUMP, B_O}));

  // Notes on the sheet:
  //   contents of rom_1 (hex, n*v repeats v):
  //   40 14 14*0 40 14 48 12 12*0 40 14 48 10 12*0 40 14 48 21 12*0 40 14 48 20 12*0 40 14 2 13*0 40 14 2
  //   13*0 40 14 14*0 40 14 14*0 40 14 14*0 40 14 14*0 40 14 14*0 40 14 a 13*0 40 14 8 13*0 40 14 80 13*0
  //   40 14 1
  //   contents of rom_2 (hex, n*v repeats v):
  //   4 8 14*0 4 8 14*0 4 8 0 20 12*0 4 8 14*0 4 8 0 1 12*0 4 8 80 13*0 4 8 c0 13*0 4 8 14*0 4 8 14*0 4 8
  //   14*0 4 8 14*0 4 8 14*0 4 8 14*0 4 8 2 13*0 4 8 14*0 4 8 10
endmodule

module L_4b_ADD (
  input  CIN,
  input  A1,
  input  B1,
  input  A2,
  input  B2,
  input  A3,
  input  B3,
  input  A4,
  input  B4,
  output Y1,
  output Y2,
  output Y3,
  output Y4,
  output COUT
);

  wire and_1_out, and_2_out, and_3_out, and_4_out, and_5_out, and_6_out, and_7_out, and_8_out, and_9_out,
       and_10_out, and_11_out, and_12_out, and_13_out, and_14_out, nand_1_out, nand_2_out, nand_3_out,
       nand_4_out, nor_1_out, nor_2_out, nor_3_out, nor_4_out, nor_5_out, nor_6_out, nor_7_out, not_1_out,
       not_2_out, not_3_out, not_4_out, not_5_out, not_6_out;

  not not_1 (not_1_out, CIN);
  nor nor_1 (nor_1_out, A1, B1);
  nand nand_1 (nand_1_out, A1, B1);
  nor nor_2 (nor_2_out, A2, B2);
  nand nand_2 (nand_2_out, A2, B2);
  nor nor_3 (nor_3_out, A3, B3);
  nand nand_3 (nand_3_out, A3, B3);
  nor nor_4 (nor_4_out, A4, B4);
  nand nand_4 (nand_4_out, A4, B4);
  not not_2 (not_2_out, not_1_out);
  not not_3 (not_3_out, nor_1_out);
  and and_1 (and_1_out, not_1_out, nand_1_out);
  not not_4 (not_4_out, nor_2_out);
  and and_2 (and_2_out, not_1_out, nand_1_out, nand_2_out);
  and and_3 (and_3_out, nand_2_out, nor_1_out);
  not not_5 (not_5_out, nor_3_out);
  and and_4 (and_4_out, not_1_out, nand_1_out, nand_2_out, nand_3_out);
  and and_5 (and_5_out, nand_2_out, nand_3_out, nor_1_out);
  and and_6 (and_6_out, nand_3_out, nor_2_out);
  not not_6 (not_6_out, nor_4_out);
  and and_7 (and_7_out, not_1_out, nand_1_out, nand_2_out, nand_3_out, nand_4_out);
  and and_8 (and_8_out, nand_2_out, nand_3_out, nand_4_out, nor_1_out);
  and and_9 (and_9_out, nand_3_out, nand_4_out, nor_2_out);
  and and_10 (and_10_out, nand_4_out, nor_3_out);
  and and_11 (and_11_out, not_3_out, nand_1_out);
  nor nor_5 (nor_5_out, and_1_out, nor_1_out);
  and and_12 (and_12_out, not_4_out, nand_2_out);
  nor nor_6 (nor_6_out, and_2_out, and_3_out, nor_2_out);
  and and_13 (and_13_out, not_5_out, nand_3_out);
  nor nor_7 (nor_7_out, and_4_out, and_5_out, and_6_out, nor_3_out);
  and and_14 (and_14_out, not_6_out, nand_4_out);
  nor nor_8 (COUT, and_7_out, and_8_out, and_10_out, nor_4_out);
  xor xor_1 (Y1, not_2_out, and_11_out);
  xor xor_2 (Y2, nor_5_out, and_12_out);
  xor xor_3 (Y3, nor_6_out, and_13_out);
  xor xor_4 (Y4, nor_7_out, and_14_out);
endmodule

module Flags_Register (
  input  in_1,
  input  in_2,
  input  [3:0] in_3,
  input  in_4,
  output [3:0] out_5
);

  C_74173 c_74173_1 (
    .D2(in_3[1]), .D3(in_3[2]), .D1(in_3[0]), .D4(in_3[3]), .CLK(in_2), .CE1(in_1), .CE2(in_1), .CLR(in_4),
    .OE1(1'b0), .OE2(1'b0), .Q2(out_5[1]), .Q3(out_5[2]), .Q1(out_5[0]), .Q4(out_5[3]));
endmodule

module Register_File (
  input  [15:0] in_1,
  input  [3:0] in_2,
  input  [3:0] in_3,
  input  in_4,
  input  in_5,
  input  in_6,
  input  [3:0] in_7,
  input  in_8,
  input  in_9,
  input  in_10,
  input  in_11,
  input  in_12,
  input  in_13
);

  wire A_IN, A_OUT, A_OUT_2, B_IN, B_OUT, B_OUT_2, C_IN, C_OUT, C_OUT_2, D_IN, D_OUT, D_OUT_2, E_IN, E_OUT,
       E_OUT_2, F_IN, F_OUT, F_OUT_2, G_IN, G_OUT, G_OUT_2, H_IN, H_OUT, H_OUT_2;
  wire [7:0] c_74273_l_1_y1, c_74273_l_2_y1, c_74273_l_3_y1, c_74273_l_4_y1, c_74273_l_5_y1, c_74273_l_6_y1,
       c_74273_l_7_y1, c_74273_l_8_y1;
  wire [15:0] c_74273_1_y1, c_74273_3_y1, c_74273_5_y1, c_74273_7_y1, controlled_buffer_1_out,
       controlled_buffer_7_out;

  C_74273_L c_74273_l_1 (
    .D2(in_1[1]), .D3(in_1[2]), .D1(in_1[0]), .D4(in_1[3]), .D5(in_1[4]), .D6(in_1[5]), .D7(in_1[6]),
    .D8(in_1[7]), .CLK(A_IN), .CLR(in_4), .Y2(c_74273_l_1_y1[1]), .Y3(c_74273_l_1_y1[2]),
    .Y1(c_74273_l_1_y1[0]), .Y4(c_74273_l_1_y1[3]), .Y5(c_74273_l_1_y1[4]), .Y6(c_74273_l_1_y1[5]),
    .Y7(c_74273_l_1_y1[6]), .Y8(c_74273_l_1_y1[7]));
  C_74273_L c_74273_l_2 (
    .D2(in_1[9]), .D3(in_1[10]), .D1(in_1[8]), .D4(in_1[11]), .D5(in_1[12]), .D6(in_1[13]), .D7(in_1[14]),
    .D8(in_1[15]), .CLK(A_IN), .CLR(in_4), .Y2(c_74273_l_2_y1[1]), .Y3(c_74273_l_2_y1[2]),
    .Y1(c_74273_l_2_y1[0]), .Y4(c_74273_l_2_y1[3]), .Y5(c_74273_l_2_y1[4]), .Y6(c_74273_l_2_y1[5]),
    .Y7(c_74273_l_2_y1[6]), .Y8(c_74273_l_2_y1[7]));
  C_74273_L c_74273_l_3 (
    .D2(in_1[1]), .D3(in_1[2]), .D1(in_1[0]), .D4(in_1[3]), .D5(in_1[4]), .D6(in_1[5]), .D7(in_1[6]),
    .D8(in_1[7]), .CLK(B_IN), .CLR(in_8), .Y2(c_74273_l_3_y1[1]), .Y3(c_74273_l_3_y1[2]),
    .Y1(c_74273_l_3_y1[0]), .Y4(c_74273_l_3_y1[3]), .Y5(c_74273_l_3_y1[4]), .Y6(c_74273_l_3_y1[5]),
    .Y7(c_74273_l_3_y1[6]), .Y8(c_74273_l_3_y1[7]));
  C_74273_L c_74273_l_4 (
    .D2(in_1[9]), .D3(in_1[10]), .D1(in_1[8]), .D4(in_1[11]), .D5(in_1[12]), .D6(in_1[13]), .D7(in_1[14]),
    .D8(in_1[15]), .CLK(B_IN), .CLR(in_8), .Y2(c_74273_l_4_y1[1]), .Y3(c_74273_l_4_y1[2]),
    .Y1(c_74273_l_4_y1[0]), .Y4(c_74273_l_4_y1[3]), .Y5(c_74273_l_4_y1[4]), .Y6(c_74273_l_4_y1[5]),
    .Y7(c_74273_l_4_y1[6]), .Y8(c_74273_l_4_y1[7]));
  C_74273_L c_74273_l_5 (
    .D2(in_1[1]), .D3(in_1[2]), .D1(in_1[0]), .D4(in_1[3]), .D5(in_1[4]), .D6(in_1[5]), .D7(in_1[6]),
    .D8(in_1[7]), .CLK(C_IN), .CLR(in_10), .Y2(c_74273_l_5_y1[1]), .Y3(c_74273_l_5_y1[2]),
    .Y1(c_74273_l_5_y1[0]), .Y4(c_74273_l_5_y1[3]), .Y5(c_74273_l_5_y1[4]), .Y6(c_74273_l_5_y1[5]),
    .Y7(c_74273_l_5_y1[6]), .Y8(c_74273_l_5_y1[7]));
  C_74273_L c_74273_l_6 (
    .D2(in_1[9]), .D3(in_1[10]), .D1(in_1[8]), .D4(in_1[11]), .D5(in_1[12]), .D6(in_1[13]), .D7(in_1[14]),
    .D8(in_1[15]), .CLK(C_IN), .CLR(in_10), .Y2(c_74273_l_6_y1[1]), .Y3(c_74273_l_6_y1[2]),
    .Y1(c_74273_l_6_y1[0]), .Y4(c_74273_l_6_y1[3]), .Y5(c_74273_l_6_y1[4]), .Y6(c_74273_l_6_y1[5]),
    .Y7(c_74273_l_6_y1[6]), .Y8(c_74273_l_6_y1[7]));
  C_74273_L c_74273_l_7 (
    .D2(in_1[1]), .D3(in_1[2]), .D1(in_1[0]), .D4(in_1[3]), .D5(in_1[4]), .D6(in_1[5]), .D7(in_1[6]),
    .D8(in_1[7]), .CLK(D_IN), .CLR(in_12), .Y2(c_74273_l_7_y1[1]), .Y3(c_74273_l_7_y1[2]),
    .Y1(c_74273_l_7_y1[0]), .Y4(c_74273_l_7_y1[3]), .Y5(c_74273_l_7_y1[4]), .Y6(c_74273_l_7_y1[5]),
    .Y7(c_74273_l_7_y1[6]), .Y8(c_74273_l_7_y1[7]));
  C_74273_L c_74273_l_8 (
    .D2(in_1[9]), .D3(in_1[10]), .D1(in_1[8]), .D4(in_1[11]), .D5(in_1[12]), .D6(in_1[13]), .D7(in_1[14]),
    .D8(in_1[15]), .CLK(D_IN), .CLR(in_12), .Y2(c_74273_l_8_y1[1]), .Y3(c_74273_l_8_y1[2]),
    .Y1(c_74273_l_8_y1[0]), .Y4(c_74273_l_8_y1[3]), .Y5(c_74273_l_8_y1[4]), .Y6(c_74273_l_8_y1[5]),
    .Y7(c_74273_l_8_y1[6]), .Y8(c_74273_l_8_y1[7]));
  assign controlled_buffer_1_out = A_OUT ? {c_74273_l_2_y1, c_74273_l_1_y1} : 16'bz;  // Controlled_Buffer controlled_buffer_1
  assign controlled_buffer_1_out = B_OUT ? {c_74273_l_4_y1, c_74273_l_3_y1} : 16'bz;  // Controlled_Buffer controlled_buffer_2
  assign controlled_buffer_1_out = C_OUT ? {c_74273_l_6_y1, c_74273_l_5_y1} : 16'bz;  // Controlled_Buffer controlled_buffer_3
  assign controlled_buffer_1_out = D_OUT ? {c_74273_l_8_y1, c_74273_l_7_y1} : 16'bz;  // Controlled_Buffer controlled_buffer_4
  Controlled_Buffer #(.width(16)) controlled_buffer_5 (.in(controlled_buffer_7_out), .out(in_1));  // open: en
  assign controlled_buffer_1_out = E_OUT ? c_74273_1_y1 : 16'bz;  // Controlled_Buffer controlled_buffer_6
  assign controlled_buffer_7_out = A_OUT_2 ? {c_74273_l_2_y1, c_74273_l_1_y1} : 16'bz;  // Controlled_Buffer controlled_buffer_7
  assign controlled_buffer_1_out = F_OUT ? c_74273_3_y1 : 16'bz;  // Controlled_Buffer controlled_buffer_8
  assign controlled_buffer_7_out = B_OUT_2 ? {c_74273_l_4_y1, c_74273_l_3_y1} : 16'bz;  // Controlled_Buffer controlled_buffer_9
  assign controlled_buffer_1_out = G_OUT ? c_74273_5_y1 : 16'bz;  // Controlled_Buffer controlled_buffer_10
  assign controlled_buffer_7_out = C_OUT_2 ? {c_74273_l_6_y1, c_74273_l_5_y1} : 16'bz;  // Controlled_Buffer controlled_buffer_11
  assign controlled_buffer_1_out = H_OUT ? c_74273_7_y1 : 16'bz;  // Controlled_Buffer controlled_buffer_12
  assign controlled_buffer_7_out = D_OUT_2 ? {c_74273_l_8_y1, c_74273_l_7_y1} : 16'bz;  // Controlled_Buffer controlled_buffer_13
  assign controlled_buffer_7_out = E_OUT_2 ? c_74273_1_y1 : 16'bz;  // Controlled_Buffer controlled_buffer_14
  assign controlled_buffer_7_out = F_OUT_2 ? c_74273_3_y1 : 16'bz;  // Controlled_Buffer controlled_buffer_15
  assign controlled_buffer_7_out = G_OUT_2 ? c_74273_5_y1 : 16'bz;  // Controlled_Buffer controlled_buffer_16
  assign controlled_buffer_7_out = H_OUT_2 ? c_74273_7_y1 : 16'bz;  // Controlled_Buffer controlled_buffer_17
  C_74273 c_74273_1 (
    .D2(in_1[1]), .D3(in_1[2]), .D1(in_1[0]), .D4(in_1[3]), .D5(in_1[4]), .D6(in_1[5]), .D7(in_1[6]),
    .D8(in_1[7]), .CLK(E_IN), .CLR(in_5), .Y2(c_74273_1_y1[1]), .Y3(c_74273_1_y1[2]), .Y1(c_74273_1_y1[0]),
    .Y4(c_74273_1_y1[3]), .Y5(c_74273_1_y1[4]), .Y6(c_74273_1_y1[5]), .Y7(c_74273_1_y1[6]),
    .Y8(c_74273_1_y1[7]));
  C_74273 c_74273_2 (
    .D2(in_1[9]), .D3(in_1[10]), .D1(in_1[8]), .D4(in_1[11]), .D5(in_1[12]), .D6(in_1[13]), .D7(in_1[14]),
    .D8(in_1[15]), .CLK(E_IN), .CLR(in_5), .Y2(c_74273_1_y1[9]), .Y3(c_74273_1_y1[10]), .Y1(c_74273_1_y1[8]),
    .Y4(c_74273_1_y1[11]), .Y5(c_74273_1_y1[12]), .Y6(c_74273_1_y1[13]), .Y7(c_74273_1_y1[14]),
    .Y8(c_74273_1_y1[15]));
  C_74273 c_74273_3 (
    .D2(in_1[1]), .D3(in_1[2]), .D1(in_1[0]), .D4(in_1[3]), .D5(in_1[4]), .D6(in_1[5]), .D7(in_1[6]),
    .D8(in_1[7]), .CLK(F_IN), .CLR(in_9), .Y2(c_74273_3_y1[1]), .Y3(c_74273_3_y1[2]), .Y1(c_74273_3_y1[0]),
    .Y4(c_74273_3_y1[3]), .Y5(c_74273_3_y1[4]), .Y6(c_74273_3_y1[5]), .Y7(c_74273_3_y1[6]),
    .Y8(c_74273_3_y1[7]));
  C_74273 c_74273_4 (
    .D2(in_1[9]), .D3(in_1[10]), .D1(in_1[8]), .D4(in_1[11]), .D5(in_1[12]), .D6(in_1[13]), .D7(in_1[14]),
    .D8(in_1[15]), .CLK(F_IN), .CLR(in_9), .Y2(c_74273_3_y1[9]), .Y3(c_74273_3_y1[10]), .Y1(c_74273_3_y1[8]),
    .Y4(c_74273_3_y1[11]), .Y5(c_74273_3_y1[12]), .Y6(c_74273_3_y1[13]), .Y7(c_74273_3_y1[14]),
    .Y8(c_74273_3_y1[15]));
  C_74273 c_74273_5 (
    .D2(in_1[1]), .D3(in_1[2]), .D1(in_1[0]), .D4(in_1[3]), .D5(in_1[4]), .D6(in_1[5]), .D7(in_1[6]),
    .D8(in_1[7]), .CLK(G_IN), .CLR(in_11), .Y2(c_74273_5_y1[1]), .Y3(c_74273_5_y1[2]), .Y1(c_74273_5_y1[0]),
    .Y4(c_74273_5_y1[3]), .Y5(c_74273_5_y1[4]), .Y6(c_74273_5_y1[5]), .Y7(c_74273_5_y1[6]),
    .Y8(c_74273_5_y1[7]));
  C_74273 c_74273_6 (
    .D2(in_1[9]), .D3(in_1[10]), .D1(in_1[8]), .D4(in_1[11]), .D5(in_1[12]), .D6(in_1[13]), .D7(in_1[14]),
    .D8(in_1[15]), .CLK(G_IN), .CLR(in_11), .Y2(c_74273_5_y1[9]), .Y3(c_74273_5_y1[10]),
    .Y1(c_74273_5_y1[8]), .Y4(c_74273_5_y1[11]), .Y5(c_74273_5_y1[12]), .Y6(c_74273_5_y1[13]),
    .Y7(c_74273_5_y1[14]), .Y8(c_74273_5_y1[15]));
  C_74273 c_74273_7 (
    .D2(in_1[1]), .D3(in_1[2]), .D1(in_1[0]), .D4(in_1[3]), .D5(in_1[4]), .D6(in_1[5]), .D7(in_1[6]),
    .D8(in_1[7]), .CLK(H_IN), .CLR(in_13), .Y2(c_74273_7_y1[1]), .Y3(c_74273_7_y1[2]), .Y1(c_74273_7_y1[0]),
    .Y4(c_74273_7_y1[3]), .Y5(c_74273_7_y1[4]), .Y6(c_74273_7_y1[5]), .Y7(c_74273_7_y1[6]),
    .Y8(c_74273_7_y1[7]));
  C_74273 c_74273_8 (
    .D2(in_1[9]), .D3(in_1[10]), .D1(in_1[8]), .D4(in_1[11]), .D5(in_1[12]), .D6(in_1[13]), .D7(in_1[14]),
    .D8(in_1[15]), .CLK(H_IN), .CLR(in_13), .Y2(c_74273_7_y1[9]), .Y3(c_74273_7_y1[10]),
    .Y1(c_74273_7_y1[8]), .Y4(c_74273_7_y1[11]), .Y5(c_74273_7_y1[12]), .Y6(c_74273_7_y1[13]),
    .Y7(c_74273_7_y1[14]), .Y8(c_74273_7_y1[15]));
  // IC_74238 ic_74238_1: pin names not known; wires that end beside it: in_2[0], in_2[1], in_2[2], 1'b0, 1'b0, in_2[3], A_OUT, B_OUT, C_OUT, D_OUT, E_OUT, F_OUT, G_OUT, H_OUT
  // IC_74238 ic_74238_2: pin names not known; wires that end beside it: in_3[0], in_3[1], in_3[2], 1'b0, 1'b0, in_3[3], A_OUT_2, B_OUT_2, C_OUT_2, D_OUT_2, E_OUT_2, F_OUT_2, G_OUT_2, H_OUT_2
  // IC_74238 ic_74238_3: pin names not known; wires that end beside it: in_7[0], in_7[1], in_7[2], 1'b0, 1'b0, in_6, A_IN, B_IN, C_IN, D_IN, E_IN, F_IN, G_IN, H_IN

  // Notes on the sheet:
  //   A REG
  //   B REG
  //   C REG
  //   D REG
  //   E REG
  //   F REG
  //   G REG
  //   H REG
endmodule

module C_74377 (
  input  D1,
  input  D2,
  input  D3,
  input  D4,
  input  D5,
  input  D6,
  input  D7,
  input  D8,
  input  CLK,
  input  EN,
  input  CLR,
  output Y1,
  output Y2,
  output Y3,
  output Y4,
  output Y5,
  output Y6,
  output Y7,
  output Y8
);

  wire and_1_out, not_1_out, not_2_out;

  not not_1 (not_1_out, EN);
  D_Flip_Flop d_ff_1 (.D(D1), .clk(and_1_out), .Q(Y1), .reset(not_2_out));  // open: Qn, preset
  D_Flip_Flop d_ff_2 (.D(D2), .clk(and_1_out), .Q(Y2), .reset(not_2_out));  // open: Qn, preset
  D_Flip_Flop d_ff_3 (.D(D3), .clk(and_1_out), .Q(Y3), .reset(not_2_out));  // open: Qn, preset
  D_Flip_Flop d_ff_4 (.D(D4), .clk(and_1_out), .Q(Y4), .reset(not_2_out));  // open: Qn, preset
  D_Flip_Flop d_ff_5 (.D(D5), .clk(and_1_out), .Q(Y5), .reset(not_2_out));  // open: Qn, preset
  D_Flip_Flop d_ff_6 (.D(D6), .clk(and_1_out), .Q(Y6), .reset(not_2_out));  // open: Qn, preset
  D_Flip_Flop d_ff_7 (.D(D7), .clk(and_1_out), .Q(Y7), .reset(not_2_out));  // open: Qn, preset
  D_Flip_Flop d_ff_8 (.D(D8), .clk(and_1_out), .Q(Y8), .reset(not_2_out));  // open: Qn, preset
  and and_1 (and_1_out, CLK, not_1_out);
  not not_2 (not_2_out, CLR);
endmodule

module SN_74162374 (
  input  in_1,
  input  in_2,
  input  in_3,
  input  in_4,
  input  in_5,
  input  in_6,
  input  in_7,
  input  in_8,
  input  in_9,
  input  in_10,
  input  in_11,
  input  in_12,
  input  in_13,
  input  in_14,
  input  in_15,
  input  in_16
);

  C_74377 c_74377_1 (
    .D2(in_15), .D3(in_14), .D1(in_16), .D4(in_13), .D5(in_12), .D6(in_11), .D7(in_10), .D8(in_9));  // open: CLR, CLK, EN, Y2, Y3, Y1, Y4, Y5, Y6, Y7, Y8
  C_74377 c_74377_2 (
    .D2(in_7), .D3(in_6), .D1(in_8), .D4(in_5), .D5(in_4), .D6(in_3));  // open: CLR, D7, D8, CLK, EN, Y2, Y3, Y1, Y4, Y5, Y6, Y7, Y8
endmodule

module C_74273 (
  input  D1,
  input  D2,
  input  D3,
  input  D4,
  input  D5,
  input  D6,
  input  D7,
  input  D8,
  input  CLK,
  input  CLR,
  output Y1,
  output Y2,
  output Y3,
  output Y4,
  output Y5,
  output Y6,
  output Y7,
  output Y8
);

  wire not_1_out;

  D_Flip_Flop d_ff_1 (.D(D1), .clk(CLK), .Q(Y1), .reset(not_1_out));  // open: Qn, preset
  D_Flip_Flop d_ff_2 (.D(D2), .clk(CLK), .Q(Y2), .reset(not_1_out));  // open: Qn, preset
  D_Flip_Flop d_ff_3 (.D(D3), .clk(CLK), .Q(Y3), .reset(not_1_out));  // open: Qn, preset
  D_Flip_Flop d_ff_4 (.D(D4), .clk(CLK), .Q(Y4), .reset(not_1_out));  // open: Qn, preset
  D_Flip_Flop d_ff_5 (.D(D5), .clk(CLK), .Q(Y5), .reset(not_1_out));  // open: Qn, preset
  D_Flip_Flop d_ff_6 (.D(D6), .clk(CLK), .Q(Y6), .reset(not_1_out));  // open: Qn, preset
  D_Flip_Flop d_ff_7 (.D(D7), .clk(CLK), .Q(Y7), .reset(not_1_out));  // open: Qn, preset
  D_Flip_Flop d_ff_8 (.D(D8), .clk(CLK), .Q(Y8), .reset(not_1_out));  // open: Qn, preset
  not not_1 (not_1_out, CLR);
endmodule

module MEM_UNIT (
  input  [15:0] DATA_A,
  input  [15:0] ADR_A,
  input  [15:0] DATA_B,
  input  [15:0] ADR_B,
  input  DATA_OE_LOW,
  input  ADR_OE_LOW,
  input  RAM_O,
  input  PRG_RUN,
  input  MANUAL_W,
  input  RAM_I,
  input  CLKE,
  output [15:0] ADR,
  output [15:0] out_13,
  output [15:0] O,
  output [15:0] ALO
);

  wire ic_7400_1_p3, ic_74157_1_p4, not_1_out, not_2_out;

  not not_1 (not_1_out, MANUAL_W);
  // IC_7400 ic_7400_1: pin names not known; wires that end beside it: RAM_I, CLKE, ic_7400_1_p3
  Ram_DATA_IO_MUX ram_data_io_mux_1 (
    .in_1(not_2_out), .in_2(DATA_OE_LOW), .in_4(DATA_B), .in_3(DATA_A), .out_5(out_13));
  not not_2 (not_2_out, PRG_RUN);
  // IC_74157 ic_74157_1: pin names not known; wires that end beside it: not_1_out, ic_7400_1_p3, PRG_RUN, ic_74157_1_p4
  L_74189_Ram l_74189_ram_1 (.in_4(out_13), .in_3(ADR), .in_2(ic_74157_1_p4), .in_1(RAM_O), .out_5(O), .out_6(ALO));
  Ram_IO_MUX ram_io_mux_1 (.in_3(ADR_A), .in_4(ADR_B), .in_1(not_2_out), .in_2(ADR_OE_LOW), .out_5(ADR));
endmodule

module C_74273_L (
  input  D1,
  input  D2,
  input  D3,
  input  D4,
  input  D5,
  input  D6,
  input  D7,
  input  D8,
  input  CLK,
  input  CLR,
  output Y1,
  output Y2,
  output Y3,
  output Y4,
  output Y5,
  output Y6,
  output Y7,
  output Y8
);

  wire not_1_out;

  D_Flip_Flop d_ff_1 (.D(D1), .clk(CLK), .Q(Y1), .reset(not_1_out));  // open: Qn, preset
  D_Flip_Flop d_ff_2 (.D(D2), .clk(CLK), .Q(Y2), .reset(not_1_out));  // open: Qn, preset
  D_Flip_Flop d_ff_3 (.D(D3), .clk(CLK), .Q(Y3), .reset(not_1_out));  // open: Qn, preset
  D_Flip_Flop d_ff_4 (.D(D4), .clk(CLK), .Q(Y4), .reset(not_1_out));  // open: Qn, preset
  D_Flip_Flop d_ff_5 (.D(D5), .clk(CLK), .Q(Y5), .reset(not_1_out));  // open: Qn, preset
  D_Flip_Flop d_ff_6 (.D(D6), .clk(CLK), .Q(Y6), .reset(not_1_out));  // open: Qn, preset
  D_Flip_Flop d_ff_7 (.D(D7), .clk(CLK), .Q(Y7), .reset(not_1_out));  // open: Qn, preset
  D_Flip_Flop d_ff_8 (.D(D8), .clk(CLK), .Q(Y8), .reset(not_1_out));  // open: Qn, preset
  not not_1 (not_1_out, CLR);
endmodule

module Octal_bus_transceiver (
  input  in_1,
  input  in_2,
  input  in_3,
  input  in_4,
  input  in_5,
  input  in_6,
  input  in_7,
  input  in_8,
  input  in_9,
  input  in_10,
  input  in_11,
  input  in_12,
  input  in_13,
  input  in_14,
  input  in_15,
  input  in_16,
  input  in_17,
  input  in_18,
  output out_19,
  output out_20,
  output out_21,
  output out_22,
  output out_23,
  output out_24,
  output out_25,
  output out_26,
  output out_27,
  output out_28,
  output out_29,
  output out_30,
  output out_31,
  output out_32,
  output out_33,
  output out_34
);

  wire and_1_out, and_2_out, not_1_out;

  assign out_20 = and_1_out ? in_2 : 1'bz;  // Controlled_Buffer controlled_buffer_1
  assign out_22 = and_1_out ? in_4 : 1'bz;  // Controlled_Buffer controlled_buffer_2
  assign out_24 = and_1_out ? in_6 : 1'bz;  // Controlled_Buffer controlled_buffer_3
  assign out_26 = and_1_out ? in_8 : 1'bz;  // Controlled_Buffer controlled_buffer_4
  assign out_28 = and_1_out ? in_10 : 1'bz;  // Controlled_Buffer controlled_buffer_5
  assign out_30 = and_1_out ? in_12 : 1'bz;  // Controlled_Buffer controlled_buffer_6
  assign out_32 = and_1_out ? in_14 : 1'bz;  // Controlled_Buffer controlled_buffer_7
  assign out_34 = and_1_out ? in_16 : 1'bz;  // Controlled_Buffer controlled_buffer_8
  and and_1 (and_1_out, in_17, not_1_out);
  not not_1 (not_1_out, in_18);
  assign out_19 = and_2_out ? in_1 : 1'bz;  // Controlled_Buffer controlled_buffer_9
  assign out_21 = and_2_out ? in_3 : 1'bz;  // Controlled_Buffer controlled_buffer_10
  assign out_23 = and_2_out ? in_5 : 1'bz;  // Controlled_Buffer controlled_buffer_11
  assign out_25 = and_2_out ? in_7 : 1'bz;  // Controlled_Buffer controlled_buffer_12
  assign out_27 = and_2_out ? in_9 : 1'bz;  // Controlled_Buffer controlled_buffer_13
  assign out_29 = and_2_out ? in_11 : 1'bz;  // Controlled_Buffer controlled_buffer_14
  assign out_31 = and_2_out ? in_13 : 1'bz;  // Controlled_Buffer controlled_buffer_15
  assign out_33 = and_2_out ? in_15 : 1'bz;  // Controlled_Buffer controlled_buffer_16
  and and_2 (and_2_out, in_17, in_18);
endmodule
